// Logisim project 1 BIT ALU.circ as structural Verilog: 1 circuit, main circuit main
module main (
  input  Cin,
  input  OPERAND1,
  input  [1:0] Opcode,
  input  OPERAND2,
  output Y,
  output Cout
);

  wire adder_1_out, and_1_out, and_2_out, multiplexer_1_out, multiplexer_3_out, not_1_out, not_2_out,
       or_1_out;

  not not_1 (not_1_out, OPERAND2);
  Multiplexer multiplexer_1 (.in0(OPERAND2), .in1(not_1_out), .out(multiplexer_1_out), .sel(and_2_out));  // open: en
  and and_1 (and_1_out, OPERAND1, multiplexer_1_out);
  or or_1 (or_1_out, OPERAND1, multiplexer_1_out);
  Adder #(.width(1)) adder_1 (
    .a(OPERAND1), .b(multiplexer_1_out), .out(adder_1_out), .cin(multiplexer_3_out), .cout(Cout));
  Multiplexer #(.select(2)) multiplexer_2 (
    .in0(and_1_out), .in1(or_1_out), .in2(adder_1_out), .in3(adder_1_out), .out(Y), .sel(Opcode));  // open: en
  not not_2 (not_2_out, Cin);
  Multiplexer multiplexer_3 (.in0(Cin), .in1(not_2_out), .out(multiplexer_3_out), .sel(and_2_out));  // open: en
  and and_2 (and_2_out, Opcode[0], Opcode[1]);

  // Notes on the sheet:
  //   Figure:1 bit ALU
endmodule
