// Logisim project 16 bit ALU Fall 2020.circ as structural Verilog: 1 circuit, main circuit main
module main (
  input  in_1,
  input  in_2,
  input  [1:0] in_3,
  input  in_4,
  output out_5
);

  wire adder_1_cout, adder_1_out, and_2_out, multiplexer_1_out, multiplexer_3_out, not_1_out, not_2_out,
       undriven;

  not not_1 (not_1_out, in_4);
  Multiplexer multiplexer_1 (.in0(in_4), .in1(not_1_out), .out(multiplexer_1_out), .sel(and_2_out));  // open: en
  Adder #(.width(1)) adder_1 (
    .a(in_2), .b(multiplexer_1_out), .out(adder_1_out), .cin(multiplexer_3_out), .cout(adder_1_cout));
  and and_1 (adder_1_out, in_2, multiplexer_1_out);
  or or_1 (adder_1_out, in_2, multiplexer_1_out);
  and and_2 (and_2_out, in_3[1], in_3[0]);
  Multiplexer #(.select(2)) multiplexer_2 (
    .in0(adder_1_out), .in1(adder_1_out), .in2(adder_1_out), .in3(adder_1_out), .out(out_5), .sel(in_3));  // open: en
  not not_2 (not_2_out, in_1);
  Multiplexer multiplexer_3 (.in0(in_1), .in1(not_2_out), .out(multiplexer_3_out), .sel(and_2_out), .en(undriven));
endmodule
