// Logisim project 16 bit ALU lab06 (1).circ as structural Verilog: 3 circuits, main circuit main
// Overflow
module main (
  input  in_1,
  input  [15:0] in_2,
  input  [15:0] in_3,
  input  [1:0] Opcode,
  output [15:0] out_5,
  output Zero,
  output Overflow,
  output Cout
);

  _16_Bit_ALU u_16_bit_alu_1 (
    .OPERAND2(in_3), .OPERAND1(in_2), .Opcode(Opcode), .Y(out_5), .Zero(Zero), .Overflow(Overflow),
    .Cout(Cout), .Cin(in_1));

  // Notes on the sheet:
  //   Figure:16 bit ALU
endmodule

module _1_bit_ALU (
  input  Cin,
  input  OPERAND1,
  input  [1:0] Opcode,
  input  OPERAND2,
  output Y,
  output Cout
);

  wire adder_1_out, and_1_out, and_2_out, multiplexer_1_out, multiplexer_3_out, not_1_out, not_2_out,
       or_1_out;

  not not_1 (not_1_out, OPERAND2);
  Multiplexer multiplexer_1 (.in0(OPERAND2), .in1(not_1_out), .out(multiplexer_1_out), .sel(and_2_out));  // open: en
  and and_1 (and_1_out, OPERAND1, multiplexer_1_out);
  or or_1 (or_1_out, OPERAND1, multiplexer_1_out);
  Adder #(.width(1)) adder_1 (
    .a(OPERAND1), .b(multiplexer_1_out), .out(adder_1_out), .cin(multiplexer_3_out), .cout(Cout));
  Multiplexer #(.select(2)) multiplexer_2 (
    .in0(and_1_out), .in1(or_1_out), .in2(adder_1_out), .in3(adder_1_out), .out(Y), .sel(Opcode));  // open: en
  not not_2 (not_2_out, Cin);
  Multiplexer multiplexer_3 (.in0(Cin), .in1(not_2_out), .out(multiplexer_3_out), .sel(and_2_out));  // open: en
  and and_2 (and_2_out, Opcode[0], Opcode[1]);

  // Notes on the sheet:
  //   Figure:1 bit ALU
endmodule

// ALU
module _16_Bit_ALU (
  input  [15:0] OPERAND2,
  input  [15:0] OPERAND1,
  input  Cin,
  input  [1:0] Opcode,
  output [15:0] Y,
  output Zero,
  output Overflow,
  output Cout
);

  wire _1_cout, _2_cout, _3_cout, _4_cout, _5_cout, _6_cout, _7_cout, _8_cout, _9_cout, _10_cout, _11_cout,
       _12_cout, _13_cout, _14_cout, _15_cout;

  _1_bit_ALU _1 (.OPERAND1(OPERAND1[0]), .Opcode(Opcode), .OPERAND2(OPERAND2[0]), .Cin(Cin), .Y(Y[0]), .Cout(_1_cout));
  _1_bit_ALU _2 (
    .OPERAND1(OPERAND1[1]), .Opcode(Opcode), .OPERAND2(OPERAND2[1]), .Cin(_1_cout), .Y(Y[1]), .Cout(_2_cout));
  _1_bit_ALU _3 (
    .OPERAND1(OPERAND1[2]), .Opcode(Opcode), .OPERAND2(OPERAND2[2]), .Cin(_2_cout), .Y(Y[2]), .Cout(_3_cout));
  _1_bit_ALU _4 (
    .OPERAND1(OPERAND1[3]), .Opcode(Opcode), .OPERAND2(OPERAND2[3]), .Cin(_3_cout), .Y(Y[3]), .Cout(_4_cout));
  _1_bit_ALU _5 (
    .OPERAND1(OPERAND1[4]), .Opcode(Opcode), .OPERAND2(OPERAND2[4]), .Cin(_4_cout), .Y(Y[4]), .Cout(_5_cout));
  _1_bit_ALU _6 (
    .OPERAND1(OPERAND1[5]), .Opcode(Opcode), .OPERAND2(OPERAND2[5]), .Cin(_5_cout), .Y(Y[5]), .Cout(_6_cout));
  _1_bit_ALU _7 (
    .OPERAND1(OPERAND1[6]), .Opcode(Opcode), .OPERAND2(OPERAND2[6]), .Cin(_6_cout), .Y(Y[6]), .Cout(_7_cout));
  _1_bit_ALU _8 (
    .OPERAND1(OPERAND1[7]), .Opcode(Opcode), .OPERAND2(OPERAND2[7]), .Cin(_7_cout), .Y(Y[7]), .Cout(_8_cout));
  _1_bit_ALU _9 (
    .OPERAND1(OPERAND1[8]), .Opcode(Opcode), .OPERAND2(OPERAND2[8]), .Cin(_8_cout), .Y(Y[8]), .Cout(_9_cout));
  _1_bit_ALU _10 (
    .OPERAND1(OPERAND1[9]), .Opcode(Opcode), .OPERAND2(OPERAND2[9]), .Cin(_9_cout), .Y(Y[9]), .Cout(_10_cout));
  _1_bit_ALU _11 (
    .OPERAND1(OPERAND1[10]), .Opcode(Opcode), .OPERAND2(OPERAND2[10]), .Cin(_10_cout), .Y(Y[10]),
    .Cout(_11_cout));
  _1_bit_ALU _12 (
    .OPERAND1(OPERAND1[11]), .Opcode(Opcode), .OPERAND2(OPERAND2[11]), .Cin(_11_cout), .Y(Y[11]),
    .Cout(_12_cout));
  _1_bit_ALU _13 (
    .OPERAND1(OPERAND1[12]), .Opcode(Opcode), .OPERAND2(OPERAND2[12]), .Cin(_12_cout), .Y(Y[12]),
    .Cout(_13_cout));
  _1_bit_ALU _14 (
    .OPERAND1(OPERAND1[13]), .Opcode(Opcode), .OPERAND2(OPERAND2[13]), .Cin(_13_cout), .Y(Y[13]),
    .Cout(_14_cout));
  _1_bit_ALU _15 (
    .OPERAND1(OPERAND1[14]), .Opcode(Opcode), .OPERAND2(OPERAND2[14]), .Cin(_14_cout), .Y(Y[14]),
    .Cout(_15_cout));
  _1_bit_ALU _16 (
    .OPERAND1(OPERAND1[15]), .Opcode(Opcode), .OPERAND2(OPERAND2[15]), .Cin(_15_cout), .Y(Y[15]), .Cout(Cout));
  xor xor_1 (Overflow, Y[14], Cout);
  nor nor_1 (Zero, Y[0], Y[1], Y[2], Y[3], Y[4], Y[5], Y[6], Y[7], Y[8], Y[9], Y[10], Y[11], Y[12], Y[13], Y[14], Y[15]);
endmodule
