// Logisim project 16 bit register.circ as structural Verilog: 2 circuits, main circuit main
module main (
  input  [3:0] Read_Register_1,
  input  [3:0] Read_Register_2,
  input  [3:0] Write_register,
  input  [15:0] write_data,
  input  regWrite,
  output [15:0] Data_1,
  output [15:0] Data_2
);

  wire clock_out;

  _16_bit_register u_16_bit_register_1 (
    .write_data(write_data), .Write_register(Write_register), .read_register_1(Read_Register_1),
    .read_register_2(Read_Register_2), .read_data_1(Data_1), .read_data_2(Data_2), .regWrite(regWrite),
    .Enable(clock_out));
  Clock clock (.out(clock_out));
endmodule

module _16_bit_register (
  input  [3:0] read_register_1,
  input  [3:0] read_register_2,
  input  [3:0] Write_register,
  input  [15:0] write_data,
  input  regWrite,
  input  Enable,
  output [15:0] read_data_1,
  output [15:0] read_data_2
);

  wire and_1_out, and_2_out, and_3_out, and_4_out, and_5_out, and_6_out, and_7_out, and_8_out, and_9_out,
       and_10_out, and_11_out, and_12_out, and_13_out, and_14_out, and_15_out, and_16_out, decoder_1_out0,
       decoder_1_out1, decoder_1_out2, decoder_1_out3, decoder_1_out4, decoder_1_out5, decoder_1_out6,
       decoder_1_out7, decoder_1_out8, decoder_1_out9, decoder_1_out10, decoder_1_out11, decoder_1_out12,
       decoder_1_out13, decoder_1_out14, decoder_1_out15;
  wire [15:0] register_1_q, register_2_q, register_3_q, register_4_q, register_5_q, register_6_q,
       register_7_q, register_8_q, register_9_q, register_10_q, register_11_q, register_12_q, register_13_q,
       register_14_q, register_15_q, register_16_q;

  Decoder #(.select(4)) decoder_1 (
    .out0(decoder_1_out0), .out1(decoder_1_out1), .out2(decoder_1_out2), .out3(decoder_1_out3),
    .out4(decoder_1_out4), .out5(decoder_1_out5), .out6(decoder_1_out6), .out7(decoder_1_out7),
    .out8(decoder_1_out8), .out9(decoder_1_out9), .out10(decoder_1_out10), .out11(decoder_1_out11),
    .out12(decoder_1_out12), .out13(decoder_1_out13), .out14(decoder_1_out14), .out15(decoder_1_out15),
    .sel(Write_register));  // open: en
  and and_1 (and_1_out, regWrite, decoder_1_out0);
  and and_2 (and_2_out, regWrite, decoder_1_out1);
  and and_3 (and_3_out, regWrite, decoder_1_out2);
  and and_4 (and_4_out, regWrite, decoder_1_out3);
  and and_5 (and_5_out, regWrite, decoder_1_out4);
  and and_6 (and_6_out, regWrite, decoder_1_out5);
  and and_7 (and_7_out, regWrite, decoder_1_out6);
  and and_8 (and_8_out, regWrite, decoder_1_out7);
  Register #(.width(16)) register_1 (.D(write_data), .Q(register_1_q), .clk(Enable), .clr(and_1_out));  // open: en
  Register #(.width(16)) register_2 (.D(write_data), .Q(register_2_q), .clk(Enable), .clr(and_2_out));  // open: en
  Register #(.width(16)) register_3 (.D(write_data), .Q(register_3_q), .clk(Enable), .clr(and_3_out));  // open: en
  Register #(.width(16)) register_4 (.D(write_data), .Q(register_4_q), .clk(Enable), .clr(and_4_out));  // open: en
  Register #(.width(16)) register_5 (.D(write_data), .Q(register_5_q), .clk(Enable), .clr(and_5_out));  // open: en
  Register #(.width(16)) register_6 (.D(write_data), .Q(register_6_q), .clk(Enable), .clr(and_6_out));  // open: en
  Register #(.width(16)) register_7 (.D(write_data), .Q(register_7_q), .clk(Enable), .clr(and_7_out));  // open: en
  Register #(.width(16)) register_8 (.D(write_data), .Q(register_8_q), .clk(Enable), .clr(and_8_out));  // open: en
  and and_9 (and_9_out, regWrite, decoder_1_out8);
  and and_10 (and_10_out, regWrite, decoder_1_out9);
  and and_11 (and_11_out, regWrite, decoder_1_out10);
  and and_12 (and_12_out, regWrite, decoder_1_out11);
  and and_13 (and_13_out, regWrite, decoder_1_out12);
  and and_14 (and_14_out, regWrite, decoder_1_out13);
  and and_15 (and_15_out, regWrite, decoder_1_out14);
  and and_16 (and_16_out, regWrite, decoder_1_out15);
  Register #(.width(16)) register_9 (.D(write_data), .Q(register_9_q), .clk(Enable), .clr(and_9_out));  // open: en
  Register #(.width(16)) register_10 (.D(write_data), .Q(register_10_q), .clk(Enable), .clr(and_10_out));  // open: en
  Register #(.width(16)) register_11 (.D(write_data), .Q(register_11_q), .clk(Enable), .clr(and_11_out));  // open: en
  Register #(.width(16)) register_12 (.D(write_data), .Q(register_12_q), .clk(Enable), .clr(and_12_out));  // open: en
  Register #(.width(16)) register_13 (.D(write_data), .Q(register_13_q), .clk(Enable), .clr(and_13_out));  // open: en
  Register #(.width(16)) register_14 (.D(write_data), .Q(register_14_q), .clk(Enable), .clr(and_14_out));  // open: en
  Register #(.width(16)) register_15 (.D(write_data), .Q(register_15_q), .clk(Enable), .clr(and_15_out));  // open: en
  Register #(.width(16)) register_16 (.D(write_data), .Q(register_16_q), .clk(Enable), .clr(and_16_out));  // open: en
  Multiplexer #(.select(4), .width(16)) multiplexer_1 (
    .in0(register_9_q), .in1(register_10_q), .in2(register_11_q), .in3(register_12_q), .in4(register_13_q),
    .in5(register_14_q), .in6(register_15_q), .in7(register_16_q), .in8(register_1_q), .in9(register_2_q),
    .in10(register_3_q), .in11(register_4_q), .in12(register_5_q), .in13(register_6_q), .in14(register_7_q),
    .in15(register_8_q), .out(read_data_1), .sel(read_register_1));  // open: en
  Multiplexer #(.select(4), .width(16)) multiplexer_2 (
    .in0(register_9_q), .in1(register_10_q), .in2(register_11_q), .in3(register_12_q), .in4(register_13_q),
    .in5(register_14_q), .in6(register_15_q), .in7(register_16_q), .in8(register_1_q), .in9(register_2_q),
    .in10(register_3_q), .in11(register_4_q), .in12(register_5_q), .in13(register_6_q), .in14(register_7_q),
    .in15(register_8_q), .out(read_data_2), .sel(read_register_2));  // open: en
endmodule
