// Logisim project 2 bit Up Down Counter with Control.circ as structural Verilog: 1 circuit, main circuit main
module main (
  input  P,
  output [1:0] out_2
);

  wire clock_1_out, xnor_1_out;

  xnor xnor_1 (xnor_1_out, P, out_2[0]);
  Clock clock_1 (.out(clock_1_out));
  T_Flip_Flop X (.clk(clock_1_out), .T(xnor_1_out), .Q(out_2[1]));  // open: Qn, preset, reset, en
  T_Flip_Flop y (.clk(clock_1_out), .T(1'b1), .Q(out_2[0]));  // open: Qn, preset, reset, en
endmodule
