// Logisim project 2 bit logic unit.circ as structural Verilog: 1 circuit, main circuit main
module main (
  input  A1,
  input  B1,
  input  [1:0] in_3,
  input  in_4,
  input  in_5,
  output out_6,
  output out_7
);

  wire and_1_out, and_2_out, not_1_out, not_2_out, or_1_out, or_2_out, xor_1_out, xor_2_out;

  and and_1 (and_1_out, A1, B1);
  not not_1 (not_1_out, A1);
  or or_1 (or_1_out, A1, B1);
  xor xor_1 (xor_1_out, A1, B1);
  not not_2 (not_2_out, in_4);
  Multiplexer #(.select(2)) multiplexer_1 (
    .in0(and_1_out), .in1(or_1_out), .in2(xor_1_out), .in3(not_1_out), .out(out_6), .sel(in_3), .en(1'b1));
  and and_2 (and_2_out, in_4, in_5);
  or or_2 (or_2_out, in_4, in_5);
  xor xor_2 (xor_2_out, in_4, in_5);
  Multiplexer #(.select(2)) multiplexer_2 (
    .in0(and_2_out), .in1(or_2_out), .in2(xor_2_out), .in3(not_2_out), .out(out_7), .sel(in_3), .en(1'b1));

  // Notes on the sheet:
  //   B0
  //   A0
  //   Figure:2 bit Arithmetic Logic Unit
endmodule
