// Logisim project 2 bit synchronous up Counter.circ as structural Verilog: 1 circuit, main circuit main
module main (
  output [1:0] out_1
);

  wire clock_1_out;

  Clock clock_1 (.out(clock_1_out));
  J_K_Flip_Flop j_k_ff_1 (.J(out_1[0]), .clk(clock_1_out), .K(out_1[0]), .Q(out_1[1]));  // open: Qn, preset, en, reset
  J_K_Flip_Flop j_k_ff_2 (.J(1'b1), .clk(clock_1_out), .K(1'b1), .Q(out_1[0]));  // open: Qn, preset, en, reset

  // Notes on the sheet:
  //   Figure: 2 bit synchronous up Counter
endmodule
