// Logisim project 2BITupdOWNcOUNTER.circ as structural Verilog: 1 circuit, main circuit main
module main (
  input  A,
  input  B,
  output [1:0] AT_1Bt_1
);

  wire CLOCK_out, not_1_out, xor_1_out;

  xor xor_1 (xor_1_out, A, B);
  not not_1 (not_1_out, B);
  Clock CLOCK (.out(CLOCK_out));
  D_Flip_Flop d_ff_1 (.clk(CLOCK_out), .D(xor_1_out), .Q(AT_1Bt_1[0]));  // open: Qn, preset, en, reset
  D_Flip_Flop d_ff_2 (.clk(CLOCK_out), .D(not_1_out), .Q(AT_1Bt_1[1]));  // open: Qn, preset, en, reset
endmodule
