// Logisim project 2BitFullAdder.circ as structural Verilog: 1 circuit, main circuit main
module main (
  input  A,
  input  B,
  input  C,
  input  in_4,
  input  in_5,
  output Sum,
  output out_7,
  output SUM2,
  output Carry2
);

  wire and_1_out, and_2_out, and_3_out, and_4_out, xor_1_out, xor_2_out;

  xor xor_1 (xor_1_out, A, B);
  and and_1 (and_1_out, A, B);
  xor xor_2 (xor_2_out, in_4, in_5);
  and and_2 (and_2_out, in_4, in_5);
  xor xor_3 (Sum, xor_1_out, C);
  and and_3 (and_3_out, xor_1_out, C);
  xor xor_4 (SUM2, xor_2_out, out_7);
  and and_4 (and_4_out, xor_2_out, out_7);
  or or_1 (out_7, and_1_out, and_3_out);
  or or_2 (Carry2, and_4_out, and_2_out);

  // Notes on the sheet:
  //   1
  //   carry1
endmodule
