// Logisim project 2BitLUJan2020.circ as structural Verilog: 1 circuit, main circuit main
module main (
  input  B0,
  input  A0,
  input  [1:0] Operation,
  input  B1,
  input  A1,
  output S0,
  output S1
);

  wire and_1_out, and_2_out, not_1_out, not_2_out, or_1_out, or_2_out, undriven, xor_1_out, xor_2_out;

  and and_1 (and_1_out, B0, A0);
  or or_1 (or_1_out, A0, B0);
  not not_1 (not_1_out, A0);
  and and_2 (and_2_out, B1, B1, A1);
  or or_2 (or_2_out, B1, A1);
  xor xor_1 (xor_1_out, B1, A1);
  not not_2 (not_2_out, A1);
  xor xor_2 (xor_2_out, A0, B0);
  Multiplexer #(.select(2)) multiplexer_1 (
    .in0(and_1_out), .in1(or_1_out), .in2(xor_2_out), .in3(not_1_out), .out(S0), .sel(Operation),
    .en(undriven));
  Multiplexer #(.select(2)) multiplexer_2 (
    .in0(and_2_out), .in1(or_2_out), .in2(xor_1_out), .in3(not_2_out), .out(S1), .sel(Operation));  // open: en
endmodule
