// Logisim project 3 bit Binary Up counter.circ as structural Verilog: 1 circuit, main circuit main
module main (
  output [2:0] Output
);

  wire and_1_out, clock_1_out;

  and and_1 (and_1_out, Output[1], Output[0]);
  Clock clock_1 (.out(clock_1_out));
  T_Flip_Flop A (.clk(clock_1_out), .T(and_1_out), .Q(Output[2]));  // open: Qn, preset, reset, en
  T_Flip_Flop B (.clk(clock_1_out), .T(Output[0]), .Q(Output[1]));  // open: Qn, preset, reset, en
  T_Flip_Flop C (.clk(clock_1_out), .T(1'b1), .Q(Output[0]));  // open: Qn, preset, reset, en
endmodule
