// Logisim project 3 bit Counter MOd 6.circ as structural Verilog: 1 circuit, main circuit main
module main (
  output [2:0] out_1
);

  wire and_1_out, and_2_out, clock_1_out, t_ff_1_qn, xor_1_out;

  xor xor_1 (xor_1_out, out_1[1], out_1[2]);
  and and_1 (and_1_out, xor_1_out, out_1[0]);
  T_Flip_Flop t_ff_1 (.clk(clock_1_out), .T(and_1_out), .Q(out_1[2]), .Qn(t_ff_1_qn));  // open: preset, reset, en
  T_Flip_Flop t_ff_2 (.clk(clock_1_out), .T(and_2_out), .Q(out_1[1]));  // open: Qn, preset, reset, en
  and and_2 (and_2_out, t_ff_1_qn, out_1[0]);
  T_Flip_Flop t_ff_3 (.clk(clock_1_out), .T(1'b1), .Q(out_1[0]));  // open: Qn, preset, reset, en
  Clock clock_1 (.out(clock_1_out));

  // Notes on the sheet:
  //   Fig:3 bit binary counter (MOD6)
  //   A
  //   T2=A'C
  //   T3=1
  //   T1=C (A ExOR B)
  //   B
  //   C
endmodule
