// Logisim project 3 bit Up Down Counter.circ as structural Verilog: 1 circuit, main circuit main
module main (
  input  in_1,
  output [2:0] out_2
);

  wire and_1_out, and_2_out, clock_1_out, not_1_out, or_1_out, t_ff_2_qn, t_ff_3_qn, xor_1_out;

  not not_1 (not_1_out, in_1);
  xor xor_1 (xor_1_out, in_1, out_2[0]);
  Clock clock_1 (.out(clock_1_out));
  T_Flip_Flop t_ff_1 (.clk(clock_1_out), .T(or_1_out), .Q(out_2[2]));  // open: Qn, preset, reset, en
  and and_1 (and_1_out, t_ff_3_qn, t_ff_2_qn, in_1);
  T_Flip_Flop t_ff_2 (.clk(clock_1_out), .T(xor_1_out), .Q(out_2[1]), .Qn(t_ff_2_qn));  // open: preset, reset, en
  and and_2 (and_2_out, out_2[1], out_2[0], not_1_out);
  T_Flip_Flop t_ff_3 (.clk(clock_1_out), .T(1'b1), .Q(out_2[0]), .Qn(t_ff_3_qn));  // open: preset, reset, en
  or or_1 (or_1_out, and_1_out, and_2_out);

  // Notes on the sheet:
  //   M
  //   Figiure:3 bit binary UpDOwn Counter
  //   B
  //   C
  //   A
endmodule
