// Logisim project 4 Bit ALU.circ as structural Verilog: 3 circuits, main circuit ALU
module ALU (
  input  f2,
  input  [3:0] A,
  input  f0,
  input  [3:0] B,
  input  f3,
  input  f1,
  output v,
  output Z,
  output Cout,
  output N,
  output [3:0] Y
);

  wire [3:0] arithmetic_unit_1_y, logic_unit_1_y, multiplexer_1_out, multiplexer_2_out, not_1_out, not_2_out;

  assign not_1_out = ~A;  // NOT_Gate not_1, 4 bits wide
  assign not_2_out = ~B;  // NOT_Gate not_2, 4 bits wide
  Multiplexer #(.width(4)) multiplexer_1 (.in0(A), .in1(not_1_out), .out(multiplexer_1_out), .sel(f0), .en(1'b1));
  Multiplexer #(.width(4)) multiplexer_2 (.in0(B), .in1(not_2_out), .out(multiplexer_2_out), .sel(f1), .en(1'b1));
  Arithmetic_Unit arithmetic_unit_1 (
    .Cin(f2), .A(multiplexer_1_out), .B(multiplexer_2_out), .Y(arithmetic_unit_1_y), .Cout(Cout), .V(v));
  Logic_Unit logic_unit_1 (.A(A), .B(multiplexer_2_out), .y(logic_unit_1_y), .f0(f0), .f2(f2));
  Multiplexer #(.width(4)) multiplexer_3 (
    .in0(arithmetic_unit_1_y), .in1(logic_unit_1_y), .out({N, Y[2:0]}), .sel(f3), .en(1'b1));
  nor nor_1 (Z, Y[0], Y[1], Y[2], N);

  assign Y[3] = N;

  // Notes on the sheet:
  //   Figure:4 bit Arithmetic Logic Unit
  //   Logic Unit
  //   Arithmetic Unit
  //   f0
  //   f2
  //   Z
endmodule

module Arithmetic_Unit (
  input  Cin,
  input  [3:0] A,
  input  [3:0] B,
  output [3:0] Y,
  output Cout,
  output V
);

  wire adder_1_cout, adder_2_cout, adder_3_cout;

  Adder #(.width(1)) adder_1 (.a(A[0]), .b(B[0]), .out(Y[0]), .cin(Cin), .cout(adder_1_cout));
  Adder #(.width(1)) adder_2 (.a(A[1]), .b(B[1]), .out(Y[1]), .cin(adder_1_cout), .cout(adder_2_cout));
  Adder #(.width(1)) adder_3 (.a(A[2]), .b(B[2]), .out(Y[2]), .cin(adder_2_cout), .cout(adder_3_cout));
  Adder #(.width(1)) adder_4 (.a(A[3]), .b(B[3]), .out(Y[3]), .cin(adder_3_cout), .cout(Cout));
  xor xor_1 (V, Cout, adder_3_cout);

  // Notes on the sheet:
  //   Figure: 4 bit Arithmetic unit
  //   Cin
  //   Cout
  //   Y
endmodule

module Logic_Unit (
  input  [3:0] A,
  input  [3:0] B,
  input  f0,
  input  f2,
  output [3:0] y
);

  wire [3:0] and_1_out, or_1_out, xor_1_out;

  assign and_1_out = A & B;  // AND_Gate and_1, 4 bits wide
  assign or_1_out = A | B;  // OR_Gate or_1, 4 bits wide
  assign xor_1_out = A ^ B;  // XOR_Gate xor_1, 4 bits wide
  Multiplexer #(.select(2), .width(4)) multiplexer_1 (
    .in0(and_1_out), .in1(or_1_out), .in2(xor_1_out), .in3(B), .out(y), .sel({f2, f0}), .en(1'b1));

  // Notes on the sheet:
  //   Figure:4 bit LOGIC UNIT
  //   Bitwise AND
  //   Bitwise OR
  //   Bitwise XOR
  //   Data Movement
endmodule
