// Logisim project 4 bit UpDown Counter.circ as structural Verilog: 1 circuit, main circuit main
module main (
  input  Up,
  input  Down,
  output A0,
  output A1,
  output A2,
  output A3
);

  wire and_1_out, and_2_out, and_3_out, and_4_out, and_5_out, and_6_out, and_7_out, button_1_out, Clock_out,
       d_ff_1_qn, d_ff_2_qn, d_ff_3_qn, not_1_out, or_1_out, or_2_out, or_3_out, or_4_out, xor_1_out,
       xor_2_out, xor_3_out, xor_4_out;

  not not_1 (not_1_out, Up);
  and and_1 (and_1_out, not_1_out, Down);
  or or_1 (or_1_out, Up, and_1_out);
  and and_2 (and_2_out, and_1_out, d_ff_1_qn);
  and and_3 (and_3_out, and_2_out, d_ff_2_qn);
  and and_4 (and_4_out, and_3_out, d_ff_3_qn);
  and and_5 (and_5_out, Up, A0);
  and and_6 (and_6_out, and_5_out, A1);
  and and_7 (and_7_out, and_6_out, A2);
  or or_2 (or_2_out, and_5_out, and_2_out);
  or or_3 (or_3_out, and_6_out, and_3_out);
  or or_4 (or_4_out, and_7_out, and_4_out);
  xor xor_1 (xor_1_out, A0, or_1_out);
  xor xor_2 (xor_2_out, A1, or_2_out);
  xor xor_3 (xor_3_out, A2, or_3_out);
  xor xor_4 (xor_4_out, A3, or_4_out);
  Clock Clock (.out(Clock_out));
  D_Flip_Flop d_ff_1 (
    .clk(Clock_out), .D(xor_1_out), .Q(A0), .Qn(d_ff_1_qn), .reset(button_1_out));  // open: preset, en
  D_Flip_Flop d_ff_2 (
    .clk(Clock_out), .D(xor_2_out), .Q(A1), .Qn(d_ff_2_qn), .reset(button_1_out));  // open: preset, en
  D_Flip_Flop d_ff_3 (
    .clk(Clock_out), .D(xor_3_out), .Q(A2), .Qn(d_ff_3_qn), .reset(button_1_out));  // open: preset, en
  D_Flip_Flop d_ff_4 (.clk(Clock_out), .D(xor_4_out), .Q(A3), .reset(button_1_out));  // open: Qn, preset, en
  Button button_1 (.out(button_1_out));

  // Notes on the sheet:
  //   Figure:4 bit Up Down Counter
endmodule
