// Logisim project 4 bit down counter.circ as structural Verilog: 1 circuit, main circuit main
module main (
  output [3:0] out_1
);

  wire and_1_out, and_2_out, clock_1_out, j_k_ff_1_qn, j_k_ff_2_qn, j_k_ff_3_qn;

  and and_1 (and_1_out, j_k_ff_3_qn, j_k_ff_2_qn);
  and and_2 (and_2_out, j_k_ff_1_qn, j_k_ff_2_qn, j_k_ff_3_qn);
  Clock clock_1 (.out(clock_1_out));
  J_K_Flip_Flop j_k_ff_1 (
    .J(and_1_out), .clk(clock_1_out), .K(and_1_out), .Q(out_1[2]), .Qn(j_k_ff_1_qn));  // open: preset, en, reset
  J_K_Flip_Flop j_k_ff_2 (
    .J(j_k_ff_3_qn), .clk(clock_1_out), .K(j_k_ff_3_qn), .Q(out_1[1]), .Qn(j_k_ff_2_qn));  // open: preset, en, reset
  J_K_Flip_Flop j_k_ff_3 (
    .J(1'b1), .clk(clock_1_out), .K(1'b1), .Q(out_1[0]), .Qn(j_k_ff_3_qn));  // open: preset, en, reset
  J_K_Flip_Flop j_k_ff_4 (
    .J(and_2_out), .clk(clock_1_out), .K(and_2_out), .Q(out_1[3]));  // open: Qn, preset, en, reset

  // Notes on the sheet:
  //   A
  //   B
  //   C
  //   D
  //   FIGURE:4 bit down counter
  //   Kd=1 Jd=1
  //   Jc=D'
  //   Kc=D'
  //   Ja=B'C'D'
  //   Ka=B'C'D'
  //   Jb=C'D'
  //   Kb=C'D'
endmodule
