// Logisim project 8 bit Arithmetic Logic Unit.circ as structural Verilog: 2 circuits, main circuit main
module main (
  input  [15:0] B,
  input  [15:0] A,
  input  [1:0] OpCode
);

  wire n1_bit_alu_1_carryout_borrowin, n1_bit_alu_2_carryout_borrowin, n1_bit_alu_3_carryout_borrowin,
       n1_bit_alu_4_carryout_borrowin, n1_bit_alu_5_carryout_borrowin, n1_bit_alu_6_carryout_borrowin,
       n1_bit_alu_7_carryout_borrowin, n1_bit_alu_8_carryout_borrowin, n1_bit_alu_9_carryout_borrowin,
       n1_bit_alu_10_carryout_borrowin, n1_bit_alu_11_carryout_borrowin, n1_bit_alu_12_carryout_borrowin,
       n1_bit_alu_13_carryout_borrowin, n1_bit_alu_14_carryout_borrowin, n1_bit_alu_15_carryout_borrowin,
       n1_bit_alu_16_carryout_borrowin, undriven, undriven_2, undriven_3, undriven_4, undriven_5, undriven_6;
  wire [15:0] n1_bit_alu_1_result;

  _1_bit_ALU u_1_bit_alu_1 (
    .Carry_In(1'b0), .A(A[8]), .B(B[0]), .Borrow_In(1'b0), .OpCode(OpCode),
    .CarryOut_BorrowIn(n1_bit_alu_1_carryout_borrowin), .Result(n1_bit_alu_1_result[0]));
  _1_bit_ALU u_1_bit_alu_2 (
    .Carry_In(n1_bit_alu_1_carryout_borrowin), .A(A[9]), .B(B[1]),
    .Borrow_In(n1_bit_alu_1_carryout_borrowin), .OpCode(OpCode),
    .CarryOut_BorrowIn(n1_bit_alu_2_carryout_borrowin), .Result(n1_bit_alu_1_result[1]));
  _1_bit_ALU u_1_bit_alu_3 (
    .Carry_In(n1_bit_alu_2_carryout_borrowin), .A(A[10]), .B(B[2]),
    .Borrow_In(n1_bit_alu_2_carryout_borrowin), .OpCode(OpCode),
    .CarryOut_BorrowIn(n1_bit_alu_3_carryout_borrowin), .Result(n1_bit_alu_1_result[2]));
  _1_bit_ALU u_1_bit_alu_4 (
    .Carry_In(n1_bit_alu_3_carryout_borrowin), .A(A[11]), .B(B[3]),
    .Borrow_In(n1_bit_alu_3_carryout_borrowin), .OpCode(OpCode),
    .CarryOut_BorrowIn(n1_bit_alu_4_carryout_borrowin), .Result(n1_bit_alu_1_result[3]));
  _1_bit_ALU u_1_bit_alu_5 (
    .Carry_In(n1_bit_alu_4_carryout_borrowin), .A(A[12]), .B(B[4]),
    .Borrow_In(n1_bit_alu_4_carryout_borrowin), .OpCode(OpCode),
    .CarryOut_BorrowIn(n1_bit_alu_5_carryout_borrowin), .Result(n1_bit_alu_1_result[4]));
  _1_bit_ALU u_1_bit_alu_6 (
    .Carry_In(n1_bit_alu_5_carryout_borrowin), .A(A[13]), .B(B[5]),
    .Borrow_In(n1_bit_alu_5_carryout_borrowin), .OpCode(OpCode),
    .CarryOut_BorrowIn(n1_bit_alu_6_carryout_borrowin), .Result(n1_bit_alu_1_result[5]));
  _1_bit_ALU u_1_bit_alu_7 (
    .Carry_In(n1_bit_alu_6_carryout_borrowin), .A(A[14]), .B(B[6]),
    .Borrow_In(n1_bit_alu_6_carryout_borrowin), .OpCode(OpCode),
    .CarryOut_BorrowIn(n1_bit_alu_7_carryout_borrowin), .Result(n1_bit_alu_1_result[6]));
  _1_bit_ALU u_1_bit_alu_8 (
    .Carry_In(n1_bit_alu_7_carryout_borrowin), .A(A[15]), .B(B[7]),
    .Borrow_In(n1_bit_alu_7_carryout_borrowin), .OpCode(OpCode),
    .CarryOut_BorrowIn(n1_bit_alu_8_carryout_borrowin), .Result(n1_bit_alu_1_result[7]));
  _1_bit_ALU u_1_bit_alu_9 (
    .Carry_In(n1_bit_alu_8_carryout_borrowin), .A(B[8]), .OpCode(OpCode),
    .CarryOut_BorrowIn(n1_bit_alu_9_carryout_borrowin), .Result(n1_bit_alu_1_result[8]));  // open: B, Borrow_In
  _1_bit_ALU u_1_bit_alu_10 (
    .Carry_In(n1_bit_alu_9_carryout_borrowin), .A(B[9]), .OpCode(OpCode),
    .CarryOut_BorrowIn(n1_bit_alu_10_carryout_borrowin), .Result(n1_bit_alu_1_result[9]));  // open: B, Borrow_In
  _1_bit_ALU u_1_bit_alu_11 (
    .Carry_In(n1_bit_alu_10_carryout_borrowin), .A(undriven), .OpCode(OpCode),
    .CarryOut_BorrowIn(n1_bit_alu_11_carryout_borrowin), .Result(n1_bit_alu_1_result[10]));  // open: B, Borrow_In
  _1_bit_ALU u_1_bit_alu_12 (
    .Carry_In(n1_bit_alu_11_carryout_borrowin), .A(undriven_2), .OpCode(OpCode),
    .CarryOut_BorrowIn(n1_bit_alu_12_carryout_borrowin), .Result(n1_bit_alu_1_result[11]));  // open: B, Borrow_In
  _1_bit_ALU u_1_bit_alu_13 (
    .Carry_In(n1_bit_alu_12_carryout_borrowin), .A(undriven_3), .OpCode(OpCode),
    .CarryOut_BorrowIn(n1_bit_alu_13_carryout_borrowin), .Result(n1_bit_alu_1_result[12]));  // open: B, Borrow_In
  _1_bit_ALU u_1_bit_alu_14 (
    .Carry_In(n1_bit_alu_13_carryout_borrowin), .A(undriven_4), .OpCode(OpCode),
    .CarryOut_BorrowIn(n1_bit_alu_14_carryout_borrowin), .Result(n1_bit_alu_1_result[13]));  // open: B, Borrow_In
  _1_bit_ALU u_1_bit_alu_15 (
    .Carry_In(n1_bit_alu_14_carryout_borrowin), .A(undriven_5), .OpCode(OpCode),
    .CarryOut_BorrowIn(n1_bit_alu_15_carryout_borrowin), .Result(n1_bit_alu_1_result[14]));  // open: B, Borrow_In
  _1_bit_ALU u_1_bit_alu_16 (
    .Carry_In(n1_bit_alu_15_carryout_borrowin), .A(undriven_6), .OpCode(OpCode),
    .CarryOut_BorrowIn(n1_bit_alu_16_carryout_borrowin), .Result(n1_bit_alu_1_result[15]));  // open: B, Borrow_In

  assign A[7:6] = {2{A[8]}};

  // Notes on the sheet:
  //   Figure:8 bit Arithmetic Logic Unit
  //   Opcode
endmodule

module _1_bit_ALU (
  input  Carry_In,
  input  A,
  input  B,
  input  Borrow_In,
  input  [1:0] OpCode,
  output Result,
  output CarryOut_BorrowIn
);

  wire adder_1_cout, adder_1_out, and_1_out, and_2_out, and_3_out, or_1_out, subtractor_1_bout,
       subtractor_1_out;

  and and_1 (and_1_out, B, A);
  or or_1 (or_1_out, A, B);
  Adder #(.width(1)) adder_1 (.a(A), .b(B), .out(adder_1_out), .cin(Carry_In), .cout(adder_1_cout));
  Subtractor #(.width(1)) subtractor_1 (
    .a(A), .b(B), .out(subtractor_1_out), .bin(Borrow_In), .bout(subtractor_1_bout));
  and and_2 (and_2_out, OpCode[1], adder_1_cout);
  and and_3 (and_3_out, subtractor_1_bout, OpCode[1]);
  Multiplexer #(.select(2)) multiplexer_1 (
    .in0(and_1_out), .in1(or_1_out), .in2(adder_1_out), .in3(subtractor_1_out), .out(Result), .sel(OpCode));  // open: en
  Multiplexer multiplexer_2 (.in0(and_2_out), .in1(and_3_out), .out(CarryOut_BorrowIn), .sel(OpCode[0]));  // open: en
endmodule
