// Logisim project ALU (2 bit) (1).circ as structural Verilog: 3 circuits, main circuit ALU 1bit
module ALU_1bit (
  input  Operand_B,
  input  Operand_A,
  input  Carry_In,
  input  Binvert,
  input  [1:0] Operation,
  output Result_0,
  output Carry0
);

  wire adder_1_out, and_1_out, multiplexer_1_out, not_1_out, or_1_out;

  not not_1 (not_1_out, Operand_B);
  Multiplexer multiplexer_1 (.in0(Operand_B), .in1(not_1_out), .out(multiplexer_1_out), .sel(Binvert));  // open: en
  and and_1 (and_1_out, Operand_A, Operand_B);
  or or_1 (or_1_out, Operand_A, Operand_B);
  Adder #(.width(1)) adder_1 (.a(Operand_A), .b(multiplexer_1_out), .out(adder_1_out), .cin(Carry_In), .cout(Carry0));
  Multiplexer #(.select(2)) multiplexer_2 (
    .in0(and_1_out), .in1(or_1_out), .in2(adder_1_out), .out(Result_0), .sel(Operation));  // open: in3, en
endmodule

// ALU
module ALU_2_bit (
  input  [1:0] Operand_B,
  input  [1:0] Operand_A,
  input  Carry_In,
  input  [1:0] Operation,
  input  Binvert,
  output [1:0] Result,
  output Carry_1
);

  wire alu_1bit_1_carry0;

  ALU_1bit alu_1bit_1 (
    .Result_0(Result[0]), .Carry0(alu_1bit_1_carry0), .Operand_B(Operand_B[0]), .Operand_A(Operand_A[0]),
    .Carry_In(Carry_In), .Binvert(Binvert), .Operation(Operation));
  ALU_1bit alu_1bit_2 (
    .Result_0(Result[1]), .Carry0(Carry_1), .Operand_B(Operand_B[1]), .Operand_A(Operand_A[1]),
    .Carry_In(alu_1bit_1_carry0), .Binvert(Binvert), .Operation(Operation));

  // Notes on the sheet:
  //   ALU 0
  //   ALU 1
endmodule

module ALU (
  input  Carry_In,
  input  [1:0] Operand_A,
  input  [1:0] Operand_B,
  input  [1:0] Operation,
  input  Binvert,
  output [1:0] Result,
  output Carry_1
);

  ALU_2_bit alu_2_bit_1 (
    .Operation(Operation), .Binvert(Binvert), .Carry_1(Carry_1), .Operand_B(Operand_B),
    .Operand_A(Operand_A), .Carry_In(Carry_In), .Result(Result));
endmodule
