// Logisim project ALU Control Ori.circ as structural Verilog
module ALU_Control (
  input  ALUOp1,
  input  ALUOp2,
  input  F5,
  input  F4,
  input  F3,
  input  F2,
  input  F1,
  input  F0,
  output x,
  output y,
  output z
);

  wire and_1_out, and_2_out, and_3_out, and_4_out, not_1_out, not_2_out, not_3_out;

  not not_1 (not_1_out, ALUOp1);
  and and_1 (and_1_out, not_1_out, ALUOp2);
  and and_2 (and_2_out, ALUOp1, F1);
  not not_2 (not_2_out, ALUOp1);
  or or_1 (y, not_2_out, not_3_out);
  not not_3 (not_3_out, F2);
  and and_3 (and_3_out, ALUOp1, F0);
  and and_4 (and_4_out, ALUOp1, F3);
  or or_2 (x, and_1_out, and_2_out);
  or or_3 (z, and_3_out, and_4_out);
endmodule
