// Logisim project ALU(2).circ as structural Verilog: 3 circuits, main circuit ALU
module ALU (
  input  [3:0] A,
  input  f0,
  input  f1,
  input  f3,
  input  [3:0] B,
  input  f2,
  output V,
  output C,
  output [3:0] out_9
);

  wire undriven;
  wire [3:0] au_1_y1, lu_1_y2, lu_2_y2, multiplexer_2_out, not_1_out, not_2_out;

  LU lu_1 (.B(multiplexer_2_out), .Y2(lu_1_y2));  // open: f0, f1, A
  assign not_1_out = ~A;  // NOT_Gate not_1, 4 bits wide
  assign not_2_out = ~B;  // NOT_Gate not_2, 4 bits wide
  Multiplexer #(.width(4)) multiplexer_1 (.in0(A), .in1(not_1_out), .out(lu_1_y2), .sel(f0));  // open: en
  Multiplexer #(.width(4)) multiplexer_2 (.in0(B), .in1(not_2_out), .out(multiplexer_2_out), .sel(f2), .en(undriven));
  AU au_1 (.f1(f1), .A(lu_1_y2), .B(multiplexer_2_out), .Y1(au_1_y1), .V(V), .Cout(C));
  LU lu_2 (.B(multiplexer_2_out), .f0(f0), .f1(f1), .Y2(lu_2_y2), .A(lu_1_y2));
  Multiplexer #(.width(4)) multiplexer_3 (.in0(au_1_y1), .in1(lu_2_y2), .out(out_9), .sel(f3));  // open: en
endmodule

// V
module AU (
  input  f1,
  input  [3:0] A,
  input  [3:0] B,
  output [3:0] Y1,
  output V,
  output Cout
);

  wire adder_1_cout, adder_2_cout, adder_3_cout;

  Adder #(.width(1)) adder_1 (.a(A[0]), .b(B[0]), .out(Y1[0]), .cin(f1), .cout(adder_1_cout));
  Adder #(.width(1)) adder_2 (.a(A[1]), .b(B[1]), .out(Y1[1]), .cin(adder_1_cout), .cout(adder_2_cout));
  Adder #(.width(1)) adder_3 (.a(A[2]), .b(B[2]), .out(Y1[2]), .cin(adder_2_cout), .cout(adder_3_cout));
  Adder #(.width(1)) adder_4 (.a(A[3]), .b(B[3]), .out(Y1[3]), .cin(adder_3_cout), .cout(Cout));
  xor xor_1 (V, Y1[2], Cout);

  // Notes on the sheet:
  //   Cout
  //   Y1
  //   V
endmodule

module LU (
  input  [3:0] B,
  input  [3:0] A,
  input  f0,
  input  f1,
  output [3:0] Y2
);

  wire [3:0] and_1_out, not_1_out, or_1_out, xor_1_out;

  assign and_1_out = A & B;  // AND_Gate and_1, 4 bits wide
  assign not_1_out = ~B;  // NOT_Gate not_1, 4 bits wide
  assign or_1_out = A | B;  // OR_Gate or_1, 4 bits wide
  assign xor_1_out = A ^ B;  // XOR_Gate xor_1, 4 bits wide
  Multiplexer #(.select(2), .width(4)) multiplexer_1 (
    .in0(and_1_out), .in1(or_1_out), .in2(xor_1_out), .in3(not_1_out), .out(Y2), .sel({f1, f0}));  // open: en
endmodule
