// Logisim project BCD 1's Complement.circ as structural Verilog: 1 circuit, main circuit main
module main (
  input  a,
  input  b,
  input  c,
  input  d,
  input  e,
  output p,
  output q,
  output r,
  output s,
  output t
);

  not not_1 (q, b);
  not not_2 (r, c);
  not not_3 (s, d);
  not not_4 (t, e);

  assign p = 1'b1;
endmodule
