// Logisim project BCD odd detector.circ as structural Verilog: 1 circuit, main circuit main
module main (
  input  A,
  input  B,
  input  C,
  input  D,
  output F
);

  not not_1 (F, D);
endmodule
