// Logisim project BinarySubtractor.circ as structural Verilog: 1 circuit, main circuit main
module main (
  input  Cin,
  input  [3:0] A,
  input  [3:0] B,
  output S0,
  output S1,
  output S2,
  output S3,
  output Cout
);

  wire adder_1_cout, adder_2_cout, adder_3_cout;
  wire [3:0] not_1_out;

  assign not_1_out = ~B;  // NOT_Gate not_1, 4 bits wide
  Adder #(.width(1)) adder_1 (.a(A[0]), .b(not_1_out[0]), .out(S0), .cin(Cin), .cout(adder_1_cout));
  Adder #(.width(1)) adder_2 (.a(A[1]), .b(not_1_out[1]), .out(S1), .cin(adder_1_cout), .cout(adder_2_cout));
  Adder #(.width(1)) adder_3 (.a(A[2]), .b(not_1_out[2]), .out(S2), .cin(adder_2_cout), .cout(adder_3_cout));
  Adder #(.width(1)) adder_4 (.a(A[3]), .b(not_1_out[3]), .out(S3), .cin(adder_3_cout), .cout(Cout));

  // Notes on the sheet:
  //   Figure:Binary Subtractor
  //   B
endmodule
