// Logisim project CPU.circ as structural Verilog: 1 circuit, main circuit main
module main (
  input  Clear
);

  wire alu_1_p4, alu_1_p6, Beq_out, Bne_out, CLK_out, control_unit_v1_1_p5, control_unit_v1_1_p8,
       control_unit_v1_1_p9, control_unit_v1_1_p10, control_unit_v1_1_p11, control_unit_v1_1_p12,
       control_unit_v1_1_p13, not_1_out, register_file_1_p4, register_file_1_p11;
  wire [1:0] control_unit_v1_1_p7;
  wire [2:0] multiplexer_1_out, register_file_1_p3;
  wire [5:0] shifter_1_out;
  wire [15:0] adder_1_out, adder_2_out, alu_1_p5, bit_extender_1_out, bit_extender_2_out, multiplexer_2_out,
       multiplexer_3_out, multiplexer_4_out, multiplexer_5_out, PC_q, ram_1_data, register_file_1_p8,
       register_file_1_p12, rom_1_data, shifter_2_out;

  Clock CLK (.out(CLK_out));
  Register #(.width(16)) PC (.D(multiplexer_5_out), .Q(PC_q), .clk(CLK_out), .clr(Clear));  // open: en
  Adder #(.width(16)) adder_1 (.a(PC_q), .b(16'h1), .out(adder_1_out));  // open: cin, cout
  ROM #(.addrWidth(16), .dataWidth(16)) rom_1 (.addr(PC_q), .data(rom_1_data));  // open: sel
  Shifter #(.width(6)) shifter_1 (.in(rom_1_data[5:0]), .\dist (3'b000), .out(shifter_1_out));
  // control_unit_v1 control_unit_v1_1: pin names not known; wires that end beside it: rom_1_data[15], rom_1_data[14], rom_1_data[13], rom_1_data[12], control_unit_v1_1_p5, control_unit_v1_1_p7[1], control_unit_v1_1_p7[0], control_unit_v1_1_p8, control_unit_v1_1_p9, control_unit_v1_1_p10, control_unit_v1_1_p11, control_unit_v1_1_p12, control_unit_v1_1_p13
  Multiplexer #(.width(3)) multiplexer_1 (
    .in0(rom_1_data[8:6]), .in1(rom_1_data[5:3]), .out(multiplexer_1_out), .sel(control_unit_v1_1_p5));  // open: en
  assign bit_extender_1_out = {{13{rom_1_data[2]}}, rom_1_data[2:0]};  // Bit_Extender bit_extender_1
  assign bit_extender_2_out = {{10{rom_1_data[5]}}, rom_1_data[5:0]};  // Bit_Extender bit_extender_2
  // Register_File register_file_1: pin names not known; wires that end beside it: register_file_1_p3[2], register_file_1_p3[1], register_file_1_p3[0], register_file_1_p4, rom_1_data[11:9], rom_1_data[8:6], multiplexer_1_out, register_file_1_p8, control_unit_v1_1_p9, CLK_out, register_file_1_p11, register_file_1_p12
  Multiplexer #(.select(2), .width(16)) multiplexer_2 (
    .in0(register_file_1_p12), .in1(bit_extender_2_out), .in2(bit_extender_1_out), .out(multiplexer_2_out),
    .sel(control_unit_v1_1_p7));  // open: in3, en
  Shifter #(.width(16)) shifter_2 (.in(bit_extender_2_out), .\dist (4'b0000), .out(shifter_2_out));
  Adder #(.width(16)) adder_2 (.a(adder_1_out), .b(shifter_2_out), .out(adder_2_out));  // open: cin, cout
  not not_1 (not_1_out, alu_1_p4);
  Multiplexer #(.width(16)) multiplexer_3 (
    .in0(adder_1_out), .in1(adder_2_out), .out(multiplexer_3_out), .sel(Beq_out));  // open: en
  and Beq (Beq_out, control_unit_v1_1_p13, alu_1_p4);
  and Bne (Bne_out, control_unit_v1_1_p12, not_1_out);
  // ALU alu_1: pin names not known; wires that end beside it: register_file_1_p11, multiplexer_2_out, register_file_1_p3, alu_1_p4, alu_1_p5, alu_1_p6
  LED Overflow (.in(alu_1_p6));
  Multiplexer #(.width(16)) multiplexer_4 (
    .in0(multiplexer_3_out), .in1(adder_2_out), .out(multiplexer_4_out), .sel(Bne_out));  // open: en
  Multiplexer #(.width(16)) multiplexer_5 (
    .in0(multiplexer_4_out), .in1({adder_1_out[15:6], shifter_1_out}), .out(multiplexer_5_out),
    .sel(register_file_1_p4));  // open: en
  RAM #(.addrWidth(16), .dataWidth(16), .bus("separate")) ram_1 (
    .addr(alu_1_p5), .din(register_file_1_p12), .data(ram_1_data), .str(control_unit_v1_1_p11),
    .clk(CLK_out), .ld(control_unit_v1_1_p10));  // open: sel, clr
  Multiplexer #(.width(16)) multiplexer_6 (
    .in0(alu_1_p5), .in1(ram_1_data), .out(register_file_1_p8), .sel(control_unit_v1_1_p8));  // open: en

  // Notes on the sheet:
  //   Instruction
  //   JUMP - -OP[0-5]
  //   contents of rom_1 (hex, n*v repeats v):
  //   a080 a0c2 14e0
  //   OP[12-15]
  //   RS[9-11]
  //   RT[6-8]
  //   RD[3-5]
  //   Shamt[0-2]
  //   IMM[0-5]
  //   RegDst
  //   RegWrite
  //   ALUSrc
  //   ALUOP
  //   MemWrite
  //   Jump
  //   Data Memory
  //   MemRead
  //   MemToReg
endmodule
