// Logisim project CSE231Project.circ as structural Verilog
module CSE231Project (
  input  X,
  input  Y,
  input  Z
);

  wire and_1_out, and_2_out, and_3_out, and_4_out, and_5_out, and_6_out, and_7_out, and_8_out, not_1_out,
       not_2_out, not_3_out, not_4_out, not_5_out, not_6_out, not_7_out, not_8_out, or_1_out, or_2_out,
       or_3_out, or_4_out, or_5_out;

  not not_1 (not_1_out, Y);
  and and_1 (and_1_out, X, Z);
  or or_1 (or_1_out, Z, Y);
  not not_2 (not_2_out, Y);
  not not_3 (not_3_out, Z);
  not not_4 (not_4_out, Y);
  not not_5 (not_5_out, Z);
  not not_6 (not_6_out, Y);
  and and_2 (and_2_out, X, Z);
  not not_7 (not_7_out, Y);
  not not_8 (not_8_out, Z);
  or or_2 (or_2_out, not_1_out, and_1_out);
  and and_3 (and_3_out, not_2_out, not_3_out);
  and and_4 (and_4_out, X, Z);
  and and_5 (and_5_out, not_4_out, not_5_out);
  and and_6 (and_6_out, X, not_6_out);
  and and_7 (and_7_out, not_7_out, not_8_out);
  and and_8 (and_8_out, X, Y, Z);
  or or_3 (or_3_out, and_3_out, and_4_out);
  or or_4 (or_4_out, and_5_out, and_6_out);
  or or_5 (or_5_out, and_7_out, and_8_out);
  _7_Segment_Display u_7_segment_display_1 (
    .g(or_5_out), .f(and_2_out), .a(or_2_out), .b(1'b1), .e(or_4_out), .d(or_3_out), .c(or_1_out), .dp(1'b0));

  // Notes on the sheet:
  //   b
  //   c
  //   a
  //   d
  //   f
  //   g
  //   e
endmodule
