// Logisim project CSE332.circ as structural Verilog: 1 circuit, main circuit Register File
module Register_File (
  input  [15:0] in_1,
  input  RegWrite,
  input  [15:0] Write_Data,
  input  [15:0] READ_DATA1,
  input  [1:0] Read_Reg1,
  input  [1:0] Write_Register_Number,
  input  [15:0] READ_DATA2,
  input  [1:0] Read_Reg2
);

  wire and_1_out, and_2_out, and_3_out, and_4_out, clock_1_out, decoder_1_out0, decoder_1_out1,
       decoder_1_out2, decoder_1_out3;
  wire [15:0] t0_q, t1_q, t2_q, zero_q;

  Decoder #(.select(2)) decoder_1 (
    .out0(decoder_1_out0), .out1(decoder_1_out1), .out2(decoder_1_out2), .out3(decoder_1_out3),
    .sel(Write_Register_Number));  // open: en
  and and_1 (and_1_out, RegWrite, decoder_1_out0);
  and and_2 (and_2_out, RegWrite, decoder_1_out1);
  and and_3 (and_3_out, RegWrite, decoder_1_out2);
  and and_4 (and_4_out, RegWrite, decoder_1_out3);
  Clock clock_1 (.out(clock_1_out));
  Register #(.width(16)) zero (.D(Write_Data), .en(and_1_out), .Q(zero_q), .clk(clock_1_out));  // open: clr
  Register #(.width(16)) t0 (.D(in_1), .en(and_2_out), .Q(t0_q), .clk(clock_1_out));  // open: clr
  Register #(.width(16)) t1 (.D(in_1), .en(and_3_out), .Q(t1_q), .clk(clock_1_out));  // open: clr
  Register #(.width(16)) t2 (.D(in_1), .en(and_4_out), .Q(t2_q), .clk(clock_1_out));  // open: clr
  Multiplexer #(.select(2), .width(16)) multiplexer_1 (
    .in0(zero_q), .in1(t0_q), .in2(t1_q), .in3(t2_q), .out(READ_DATA1), .sel(Read_Reg1));  // open: en
  Multiplexer #(.select(2), .width(16)) multiplexer_2 (
    .in0(zero_q), .in1(t0_q), .in2(t0_q), .in3(t2_q), .out(READ_DATA2), .sel(Read_Reg2));  // open: en

  // Notes on the sheet:
  //   Fig:Register File
endmodule
