// Logisim project CSE332Project.circ as structural Verilog: 5 circuits, main circuit Register File
module Register_File (
  input  [15:0] in_1,
  input  RegWrite,
  input  [15:0] Write_Data,
  input  [15:0] READ_DATA1,
  input  [1:0] Read_Reg1,
  input  [1:0] Write_Register_Number,
  input  [15:0] READ_DATA2,
  input  [1:0] Read_Reg2
);

  wire and_1_out, and_2_out, and_3_out, and_4_out, clock_out, decoder_1_out0, decoder_1_out1, decoder_1_out2,
       decoder_1_out3;
  wire [15:0] t0_q, t1_q, t2_q, zero_q;

  Decoder #(.select(2)) decoder_1 (
    .out0(decoder_1_out0), .out1(decoder_1_out1), .out2(decoder_1_out2), .out3(decoder_1_out3),
    .sel(Write_Register_Number));  // open: en
  and and_1 (and_1_out, RegWrite, decoder_1_out0);
  and and_2 (and_2_out, RegWrite, decoder_1_out1);
  and and_3 (and_3_out, RegWrite, decoder_1_out2);
  and and_4 (and_4_out, RegWrite, decoder_1_out3);
  Clock clock (.out(clock_out));
  Register #(.width(16)) zero (.D(Write_Data), .en(and_1_out), .Q(zero_q), .clk(clock_out));  // open: clr
  Register #(.width(16)) t0 (.D(in_1), .en(and_2_out), .Q(t0_q), .clk(clock_out));  // open: clr
  Register #(.width(16)) t1 (.D(in_1), .en(and_3_out), .Q(t1_q), .clk(clock_out));  // open: clr
  Register #(.width(16)) t2 (.D(in_1), .en(and_4_out), .Q(t2_q), .clk(clock_out));  // open: clr
  Multiplexer #(.select(2), .width(16)) multiplexer_1 (
    .in0(zero_q), .in1(t0_q), .in2(t1_q), .in3(t2_q), .out(READ_DATA1), .sel(Read_Reg1));  // open: en
  Multiplexer #(.select(2), .width(16)) multiplexer_2 (
    .in0(zero_q), .in1(t0_q), .in2(t0_q), .in3(t2_q), .out(READ_DATA2), .sel(Read_Reg2));  // open: en

  // Notes on the sheet:
  //   Fig:Register File
endmodule

// b7
module _1_bit_ALU (
  input  A,
  input  B,
  input  Carry_In,
  input  BorrowIn,
  input  [1:0] Operation,
  output Result,
  output CarryOut_Borrow
);

  wire adder_1_cout, adder_1_out, and_1_out, and_2_out, and_3_out, or_1_out, subtractor_1_bout,
       subtractor_1_out, undriven;

  and and_1 (and_1_out, A, B);
  or or_1 (or_1_out, A, B);
  Adder #(.width(1)) adder_1 (.a(A), .b(B), .out(adder_1_out), .cin(Carry_In), .cout(adder_1_cout));
  Subtractor #(.width(1)) subtractor_1 (.a(A), .b(B), .out(subtractor_1_out), .bin(BorrowIn), .bout(subtractor_1_bout));
  and and_2 (and_2_out, Operation[1], adder_1_cout);
  and and_3 (and_3_out, subtractor_1_bout, Operation[1]);
  Multiplexer #(.select(2)) multiplexer_1 (
    .in0(and_1_out), .in1(or_1_out), .in2(adder_1_out), .in3(subtractor_1_out), .out(Result), .sel(Operation));  // open: en
  Multiplexer multiplexer_2 (
    .in0(and_2_out), .in1(and_3_out), .out(CarryOut_Borrow), .sel(Operation[0]), .en(undriven));

  // Notes on the sheet:
  //   BorrowIn
  //   A
  //   B
endmodule

// a14
module _16_bit_ALU (
  input  [1:0] Operation,
  input  [15:0] A,
  input  [15:0] B,
  output [15:0] Result,
  output ZERO,
  output CarryOut_borrrow
);

  wire a0_carryout_borrow, a8_carryout_borrow, a11_carryout_borrow, a14_carryout_borrow, b1_carryout_borrow,
       b4_carryout_borrow, b5_carryout_borrow, b6_carryout_borrow, b7_carryout_borrow, b9_carryout_borrow,
       b10_carryout_borrow, b11_carryout_borrow, b12_carryout_borrow, b13_carryout_borrow,
       b14_carryout_borrow;

  _1_bit_ALU a0 (
    .A(A[0]), .B(B[0]), .Carry_In(1'b0), .BorrowIn(1'b0), .Operation(Operation), .Result(Result[0]),
    .CarryOut_Borrow(a0_carryout_borrow));
  _1_bit_ALU b1 (
    .A(A[1]), .B(B[1]), .Carry_In(a0_carryout_borrow), .BorrowIn(a0_carryout_borrow), .Operation(Operation),
    .Result(Result[1]), .CarryOut_Borrow(b1_carryout_borrow));
  _1_bit_ALU a11 (
    .A(A[5]), .B(B[2]), .Carry_In(b1_carryout_borrow), .BorrowIn(b1_carryout_borrow), .Operation(Operation),
    .Result(Result[2]), .CarryOut_Borrow(a11_carryout_borrow));
  _1_bit_ALU a14 (
    .A(A[3]), .B(B[3]), .Carry_In(a11_carryout_borrow), .BorrowIn(a11_carryout_borrow),
    .Operation(Operation), .Result(Result[3]), .CarryOut_Borrow(a14_carryout_borrow));
  _1_bit_ALU b4 (
    .A(A[4]), .B(B[4]), .Carry_In(a14_carryout_borrow), .BorrowIn(a14_carryout_borrow),
    .Operation(Operation), .Result(Result[4]), .CarryOut_Borrow(b4_carryout_borrow));
  _1_bit_ALU b5 (
    .A(A[5]), .B(B[5]), .Carry_In(b4_carryout_borrow), .BorrowIn(b4_carryout_borrow), .Operation(Operation),
    .Result(Result[5]), .CarryOut_Borrow(b5_carryout_borrow));
  _1_bit_ALU b6 (
    .A(A[6]), .B(B[6]), .Carry_In(b5_carryout_borrow), .BorrowIn(b5_carryout_borrow), .Operation(Operation),
    .Result(Result[6]), .CarryOut_Borrow(b6_carryout_borrow));
  _1_bit_ALU b7 (
    .A(A[7]), .B(B[7]), .Carry_In(b6_carryout_borrow), .BorrowIn(b6_carryout_borrow), .Operation(Operation),
    .Result(Result[7]), .CarryOut_Borrow(b7_carryout_borrow));
  _1_bit_ALU a8 (
    .A(A[8]), .B(B[8]), .Carry_In(b7_carryout_borrow), .BorrowIn(b7_carryout_borrow), .Operation(Operation),
    .Result(Result[8]), .CarryOut_Borrow(a8_carryout_borrow));
  _1_bit_ALU b9 (
    .A(A[9]), .B(B[9]), .Carry_In(a8_carryout_borrow), .BorrowIn(a8_carryout_borrow), .Operation(Operation),
    .Result(Result[9]), .CarryOut_Borrow(b9_carryout_borrow));
  _1_bit_ALU b10 (
    .A(A[10]), .B(B[10]), .Carry_In(b9_carryout_borrow), .BorrowIn(b9_carryout_borrow),
    .Operation(Operation), .Result(Result[10]), .CarryOut_Borrow(b10_carryout_borrow));
  _1_bit_ALU b11 (
    .A(A[11]), .B(B[11]), .Carry_In(b10_carryout_borrow), .BorrowIn(b10_carryout_borrow),
    .Operation(Operation), .Result(Result[11]), .CarryOut_Borrow(b11_carryout_borrow));
  _1_bit_ALU b12 (
    .A(A[12]), .B(B[12]), .Carry_In(b11_carryout_borrow), .BorrowIn(b11_carryout_borrow),
    .Operation(Operation), .Result(Result[12]), .CarryOut_Borrow(b12_carryout_borrow));
  _1_bit_ALU b13 (
    .A(A[13]), .B(B[13]), .Carry_In(b12_carryout_borrow), .BorrowIn(b12_carryout_borrow),
    .Operation(Operation), .Result(Result[13]), .CarryOut_Borrow(b13_carryout_borrow));
  _1_bit_ALU b14 (
    .A(A[14]), .B(B[14]), .Carry_In(b13_carryout_borrow), .BorrowIn(b13_carryout_borrow),
    .Operation(Operation), .Result(Result[14]), .CarryOut_Borrow(b14_carryout_borrow));
  _1_bit_ALU b15 (
    .A(A[15]), .B(B[15]), .Carry_In(b14_carryout_borrow), .BorrowIn(b14_carryout_borrow),
    .Operation(Operation), .Result(Result[15]), .CarryOut_Borrow(CarryOut_borrrow));
  nor nor_1 (ZERO, Result[15], Result[14], Result[13], Result[12], Result[11], Result[10], Result[9], Result[8], Result[7], Result[6], Result[5], Result[3], Result[4], Result[2], Result[1], Result[0]);

  assign A[2] = A[5];

  // Other names for the same wires on the sheet: a2 = A[5]

  // Notes on the sheet:
  //   1
  //   2
  //   3
  //   4
  //   5
  //   6
  //   12
  //   15
  //   0
  //   7
  //   8
  //   9
  //   10
  //   11
  //   13
  //   14
  //   9
  //   10
endmodule

module Datapath (
  input  in_1,
  output [9:0] Instruction
);

  wire clock_1_out, controlunit_1_alusrc, controlunit_1_memtoreg, controlunit_1_readsignal,
       controlunit_1_writesignal, n16_bit_alu_1_p4;
  wire [3:0] adder_1_out, adder_2_out, multiplexer_2_out, PC_q;
  wire [15:0] bit_extender_1_out, multiplexer_1_out, multiplexer_3_out, n16_bit_alu_1_p1, n16_bit_alu_1_p5,
       ram_1_data, undriven;

  Clock clock_1 (.out(clock_1_out));
  Register #(.width(4)) PC (.D(adder_1_out), .Q(PC_q), .clk(clock_1_out), .clr(in_1));  // open: en
  Adder #(.width(4)) adder_1 (.a(PC_q), .b(4'b0001), .out(adder_1_out));  // open: cin, cout
  ROM #(.addrWidth(4), .dataWidth(10)) rom_1 (.addr(PC_q), .data(Instruction));  // open: sel
  ControlUnit controlunit_1 (
    .OP3(Instruction[9]), .OP2(Instruction[8]), .OP1(Instruction[7]), .OP0(Instruction[6]),
    .ALUSrc(controlunit_1_alusrc), .MemtoReg(controlunit_1_memtoreg),
    .WriteSignal(controlunit_1_writesignal), .ReadSignal(controlunit_1_readsignal));
  Register_File register_file_1 (
    .Write_Data(multiplexer_3_out), .Read_Reg1(Instruction[5:4]), .Write_Register_Number(Instruction[1:0]),
    .Read_Reg2(Instruction[3:2]), .READ_DATA1(n16_bit_alu_1_p1), .READ_DATA2(undriven));  // open: in_1, RegWrite
  assign bit_extender_1_out = {{14{Instruction[1]}}, Instruction[1:0]};  // Bit_Extender bit_extender_1
  Multiplexer #(.width(16)) multiplexer_1 (
    .in0(undriven), .in1(bit_extender_1_out), .out(multiplexer_1_out), .sel(controlunit_1_alusrc));  // open: en
  // _16_bit_ALU 16_bit_alu_1: pin names not known; wires that end beside it: n16_bit_alu_1_p1, multiplexer_1_out, Instruction[7:6], n16_bit_alu_1_p4, n16_bit_alu_1_p5
  Adder #(.width(4)) adder_2 (.a(adder_1_out), .b(4'b0001), .out(adder_2_out));  // open: cin, cout
  Multiplexer #(.width(4)) multiplexer_2 (
    .in0(adder_1_out), .in1(adder_2_out), .out(multiplexer_2_out), .sel(n16_bit_alu_1_p4));  // open: en
  RAM #(.addrWidth(16), .dataWidth(16), .bus("separate")) ram_1 (
    .addr(n16_bit_alu_1_p5), .din(undriven), .data(ram_1_data), .str(controlunit_1_writesignal),
    .ld(controlunit_1_readsignal));  // open: sel, clk, clr
  Multiplexer #(.width(16)) multiplexer_3 (
    .in0(n16_bit_alu_1_p5), .in1(ram_1_data), .out(multiplexer_3_out), .sel(controlunit_1_memtoreg));  // open: en

  // Other names for the same wires on the sheet: rd_immediate[1:0] = Instruction[1:0]; rs[1:0] = Instruction[5:4];
  //   rt[1:0] = Instruction[3:2]

  // Notes on the sheet:
  //   R-Format
  //   OpCode rs rt rd 
  //   I -Format
  //   OpCode rs rt 
  //   4
  //   immediate
  //   2
  //   2 
  //   2
  //   INSTRUCTION FETCH
  //   OpCode
  //   0010-add
  //   0110-addi
  //   0111-lw
  //   0011-beq
  //   contents of rom_1 (hex, n*v repeats v):
  //   1c4 82 43 e4 af af 1a9 cb 4d
  //   OpCode
  //   0001
  //   - sw
  //   ALUSRC
  //   WriteSignal
  //   DATA MEMORY
  //   ReadSignal
  //   MemtoReg
endmodule

// ALUSrc
module ControlUnit (
  input  OP3,
  input  OP2,
  input  OP1,
  input  OP0,
  output ALUSrc,
  output MemtoReg,
  output WriteSignal,
  output ReadSignal
);

  wire and_1_out, not_1_out, not_2_out;

  not not_1 (not_1_out, OP1);
  and and_1 (and_1_out, OP2, OP0);
  not not_2 (not_2_out, OP1);
  or or_1 (MemtoReg, not_2_out, OP0);
  not not_3 (WriteSignal, OP1);
  and and_2 (ReadSignal, OP2, OP0);
  or or_2 (ALUSrc, not_1_out, and_1_out);
endmodule
