// Logisim project Canonical Form1.circ as structural Verilog: 1 circuit, main circuit main
module main (
  input  A,
  input  B,
  input  C,
  output out_4
);

  wire and_1_out, and_2_out, not_1_out, not_2_out, not_3_out;

  not not_1 (not_1_out, B);
  not not_2 (not_2_out, A);
  not not_3 (not_3_out, C);
  and and_1 (and_1_out, not_1_out, C);
  and and_2 (and_2_out, B, not_3_out, 1'b1);
  or or_1 (out_4, and_1_out, and_2_out, 1'b0);

  // Notes on the sheet:
  //   Name:Rownita Tasneem
  //   ID #1813153642
endmodule
