// Logisim project CustomizedALU.circ as structural Verilog: 3 circuits, main circuit main
module main (
  input  [2:0] OpCode,
  input  [7:0] A,
  input  [7:0] B,
  output [7:0] Output,
  output V,
  output Z,
  output N
);

  _8_bit_ALU u_8_bit_alu_1 (.Y(Output), .N(N), .Z(Z), .V(V), .A(A), .B(B), .OpCode(OpCode));  // open: Cout
endmodule

module _1_bit_ALU (
  input  Cin,
  input  Binvert,
  input  [1:0] Operation,
  input  A,
  input  B,
  output Y,
  output Cout
);

  wire adder_1_out, and_1_out, multiplexer_1_out, not_1_out, or_1_out;

  not not_1 (not_1_out, B);
  Multiplexer multiplexer_1 (.in0(B), .in1(not_1_out), .out(multiplexer_1_out), .sel(Binvert));  // open: en
  and and_1 (and_1_out, A, multiplexer_1_out);
  or or_1 (or_1_out, A, multiplexer_1_out);
  Adder #(.width(1)) adder_1 (.a(A), .b(multiplexer_1_out), .out(adder_1_out), .cin(Cin), .cout(Cout));
  Multiplexer #(.select(2)) multiplexer_2 (
    .in0(and_1_out), .in1(or_1_out), .in2(adder_1_out), .out(Y), .sel(Operation));  // open: in3, en

  // Notes on the sheet:
  //   If Binvwert=0,then we have to add two numbers.So,Cin=0 
  //   If Binvert=1,then we have to subtract two numbers.Then Cin=1 
  //   Designing A 1 bit ALU that can do the AND,OR ,add and sub functions
  //   ADD
  //   SUB
  //   AND
  //   OR
  //   0
  //   1
  //   Functions  Binvert Operation
  //   0
  //   0
  //   10
  //   10
  //   00
  //   A ll B
  //   01
  //   A+B
  //   A - B
  //   A && B
endmodule

// Z
module _8_bit_ALU (
  input  [2:0] OpCode,
  input  [7:0] A,
  input  [7:0] B,
  output [7:0] Y,
  output N,
  output Z,
  output V,
  output Cout
);

  wire n1_bit_alu_1_cout, n1_bit_alu_2_cout, n1_bit_alu_3_cout, n1_bit_alu_4_cout, n1_bit_alu_5_cout,
       n1_bit_alu_6_cout, n1_bit_alu_7_cout;

  _1_bit_ALU u_1_bit_alu_1 (
    .Binvert(OpCode[2]), .Operation(OpCode[1:0]), .Y(Y[0]), .Cout(n1_bit_alu_1_cout), .A(A[0]), .B(B[0]),
    .Cin(OpCode[2]));
  _1_bit_ALU u_1_bit_alu_2 (
    .Binvert(OpCode[2]), .Operation(OpCode[1:0]), .Y(Y[1]), .Cout(n1_bit_alu_2_cout), .A(A[1]), .B(B[1]),
    .Cin(n1_bit_alu_1_cout));
  _1_bit_ALU u_1_bit_alu_3 (
    .Binvert(OpCode[2]), .Operation(OpCode[1:0]), .Y(Y[2]), .Cout(n1_bit_alu_3_cout), .A(A[2]), .B(B[2]),
    .Cin(n1_bit_alu_2_cout));
  _1_bit_ALU u_1_bit_alu_4 (
    .Binvert(OpCode[2]), .Operation(OpCode[1:0]), .Y(Y[3]), .Cout(n1_bit_alu_4_cout), .A(A[3]), .B(B[3]),
    .Cin(n1_bit_alu_3_cout));
  _1_bit_ALU u_1_bit_alu_5 (
    .Binvert(OpCode[2]), .Operation(OpCode[1:0]), .Y(Y[4]), .Cout(n1_bit_alu_5_cout), .A(A[4]), .B(B[4]),
    .Cin(n1_bit_alu_4_cout));
  _1_bit_ALU u_1_bit_alu_6 (
    .Binvert(OpCode[2]), .Operation(OpCode[1:0]), .Y(Y[5]), .Cout(n1_bit_alu_6_cout), .A(A[5]), .B(B[5]),
    .Cin(n1_bit_alu_5_cout));
  _1_bit_ALU u_1_bit_alu_7 (
    .Binvert(OpCode[2]), .Operation(OpCode[1:0]), .Y(Y[6]), .Cout(n1_bit_alu_7_cout), .A(A[6]), .B(B[6]),
    .Cin(n1_bit_alu_6_cout));
  _1_bit_ALU u_1_bit_alu_8 (
    .Binvert(OpCode[2]), .Operation(OpCode[1:0]), .Y(N), .Cout(Cout), .A(A[7]), .B(B[7]),
    .Cin(n1_bit_alu_7_cout));
  xor xor_1 (V, n1_bit_alu_7_cout, Cout);
  nor nor_1 (Z, Y[0], Y[1], Y[2], Y[4], Y[6], Y[3], N, Y[5]);

  assign Y[7] = N;
endmodule
