// Logisim project D To T FLIPFLOP CONVERSION.circ as structural Verilog: 1 circuit, main circuit main
module main (
  input  T,
  output Q,
  output Q_prime
);

  wire clock_1_out, xor_1_out;

  Clock clock_1 (.out(clock_1_out));
  xor xor_1 (xor_1_out, T, Q);
  D_Flip_Flop d_ff_1 (.clk(clock_1_out), .D(xor_1_out), .Q(Q), .Qn(Q_prime));  // open: preset, en, reset

  // Notes on the sheet:
  //   FIGURE: D FF TO T FF CONVERSION
endmodule
