// Logisim project DatapathLab07Old.circ as structural Verilog: 1 circuit, main circuit main
module main (
  input  Cin,
  input  [15:0] Result,
  input  RegWrite,
  input  in_4,
  output [15:0] out_5,
  output Overflow,
  output Zero,
  output Cout
);

  wire CLK_out;
  wire [1:0] bit_extender_2_out;
  wire [3:0] multiplexer_1_out, RT;
  wire [7:0] adder_1_out, register_1_q;
  wire [15:0] ID, multiplexer_2_out, n16_bit_register_1_read_data_1, n16_bit_register_1_read_data_2;

  Register register_1 (.D(adder_1_out), .Q(register_1_q), .clk(CLK_out), .clr(in_4));  // open: en
  Adder adder_1 (.a(8'h1), .b(register_1_q), .out(adder_1_out));  // open: cin, cout
  ROM #(.dataWidth(16)) rom_1 (.addr(register_1_q), .data(out_5));  // open: sel
  Multiplexer #(.width(4)) multiplexer_1 (
    .in0(out_5[3:0]), .in1(RT), .out(multiplexer_1_out), .sel(out_5[14]));  // open: en
  Clock CLK (.out(CLK_out));
  _16_bit_register u_16_bit_register_1 (
    .write_data(Result), .Write_register(multiplexer_1_out), .read_register_1(out_5[11:8]),
    .read_register_2(out_5[7:4]), .read_data_1(n16_bit_register_1_read_data_1),
    .read_data_2(n16_bit_register_1_read_data_2), .regWrite(RegWrite), .Enable(CLK_out));
  assign ID = {{12{1'b0}}, out_5[3:0]};  // Bit_Extender bit_extender_1
  _16_Bit_ALU u_Cin (
    .OPERAND2(multiplexer_2_out), .OPERAND1(n16_bit_register_1_read_data_1), .Opcode(bit_extender_2_out),
    .Y(Result), .Zero(Overflow), .Overflow(Zero), .Cout(Cout), .Cin(Cin));
  Multiplexer #(.width(16)) multiplexer_2 (
    .in0(n16_bit_register_1_read_data_2), .in1(ID), .out(multiplexer_2_out), .sel(out_5[14]));  // open: en
  Bit_Extender #(.in_width(4), .out_width(2)) bit_extender_2 (.in(out_5[15:12]), .out(bit_extender_2_out));

  // Other names for the same wires on the sheet: RD[3:0] = out_5[3:0]; Rt_t[3:0] = out_5[7:4]; Rs[3:0] = out_5[11:8];
  //   Op[3:0] = out_5[15:12]

  // Notes on the sheet:
  //   contents of rom_1 (hex, n*v repeats v):
  //   2123
endmodule
