// Logisim project DisplayingNumbers.circ as structural Verilog: 1 circuit, main circuit main
module main (
  input  w,
  input  x,
  input  y,
  input  z
);

  wire and_1_out, and_2_out, and_3_out, and_4_out, and_5_out, and_6_out, and_7_out, and_8_out, and_9_out,
       and_10_out, and_11_out, and_12_out, and_13_out, and_14_out, and_15_out, and_16_out, and_17_out,
       and_18_out, and_19_out, and_20_out, and_21_out, not_1_out, not_2_out, not_3_out, not_4_out, not_5_out,
       not_6_out, not_7_out, not_8_out, not_9_out, not_10_out, not_11_out, not_12_out, not_13_out,
       not_14_out, not_15_out, not_16_out, not_17_out, not_18_out, not_19_out, not_20_out, not_21_out,
       not_22_out, not_23_out, not_24_out, not_25_out, not_26_out, not_27_out, not_28_out, not_29_out,
       not_30_out, not_31_out, not_32_out, not_33_out, not_34_out, not_35_out, not_36_out, not_37_out,
       not_38_out, not_39_out, not_40_out, not_41_out, or_1_out, or_2_out, or_3_out, or_4_out, or_5_out;

  not not_1 (not_1_out, w);
  not not_2 (not_2_out, w);
  not not_3 (not_3_out, w);
  not not_4 (not_4_out, x);
  not not_5 (not_5_out, y);
  not not_6 (not_6_out, z);
  not not_7 (not_7_out, w);
  not not_8 (not_8_out, x);
  and and_1 (and_1_out, not_8_out, not_9_out, not_10_out);
  not not_9 (not_9_out, y);
  not not_10 (not_10_out, z);
  not not_11 (not_11_out, w);
  and and_2 (and_2_out, not_11_out, z);
  not not_12 (not_12_out, w);
  and and_3 (and_3_out, not_12_out, y);
  not not_13 (not_13_out, w);
  not not_14 (not_14_out, y);
  not not_15 (not_15_out, w);
  not not_16 (not_16_out, z);
  not not_17 (not_17_out, w);
  not not_18 (not_18_out, x);
  not not_19 (not_19_out, y);
  not not_20 (not_20_out, z);
  not not_21 (not_21_out, w);
  and and_4 (and_4_out, not_21_out, x, not_22_out);
  not not_22 (not_22_out, z);
  not not_23 (not_23_out, w);
  not not_24 (not_24_out, y);
  not not_25 (not_25_out, w);
  not not_26 (not_26_out, z);
  not not_27 (not_27_out, w);
  not not_28 (not_28_out, x);
  not not_29 (not_29_out, y);
  not not_30 (not_30_out, z);
  not not_31 (not_31_out, w);
  not not_32 (not_32_out, y);
  not not_33 (not_33_out, w);
  not not_34 (not_34_out, x);
  not not_35 (not_35_out, z);
  not not_36 (not_36_out, w);
  not not_37 (not_37_out, y);
  not not_38 (not_38_out, w);
  not not_39 (not_39_out, x);
  not not_40 (not_40_out, y);
  not not_41 (not_41_out, z);
  and and_5 (and_5_out, not_1_out, z);
  and and_6 (and_6_out, not_2_out, y);
  and and_7 (and_7_out, not_3_out, x);
  and and_8 (and_8_out, w, not_4_out, not_5_out, not_6_out);
  or or_1 (or_1_out, and_1_out, and_2_out, and_3_out);
  and and_9 (and_9_out, not_13_out, not_14_out, z);
  and and_10 (and_10_out, not_15_out, y, not_16_out);
  and and_11 (and_11_out, not_17_out, x);
  and and_12 (and_12_out, w, not_18_out, not_19_out, not_20_out);
  and and_13 (and_13_out, not_23_out, not_24_out, z);
  and and_14 (and_14_out, not_25_out, y, not_26_out);
  and and_15 (and_15_out, not_27_out, x, y);
  and and_16 (and_16_out, w, not_28_out, not_29_out, not_30_out);
  and and_17 (and_17_out, not_31_out, not_32_out, z);
  and and_18 (and_18_out, not_33_out, not_34_out, y, not_35_out);
  and and_19 (and_19_out, not_36_out, x, not_37_out);
  and and_20 (and_20_out, not_38_out, x, z);
  and and_21 (and_21_out, w, not_39_out, not_40_out, not_41_out);
  or or_2 (or_2_out, and_5_out, and_6_out, and_7_out, and_8_out);
  or or_3 (or_3_out, and_9_out, and_10_out, and_11_out, and_12_out);
  or or_4 (or_4_out, and_13_out, and_14_out, and_15_out, and_16_out);
  or or_5 (or_5_out, and_17_out, and_18_out, and_19_out, and_20_out, and_21_out);
  _7_Segment_Display u_7_segment_display_1 (
    .g(or_5_out), .f(or_4_out), .a(or_2_out), .b(not_7_out), .e(and_4_out), .d(or_3_out), .c(or_1_out),
    .dp(1'b0));

  // Notes on the sheet:
  //   b
  //   e
  //   f
  //   g
  //   h
  //   a
  //   c
  //   d
endmodule
