// Logisim project Encoder001.circ as structural Verilog: 1 circuit, main circuit main
module main (
  input  D0,
  input  D1,
  input  D2,
  input  D3,
  input  D4,
  input  D5,
  input  D6,
  input  D7,
  output out_9,
  output out_10,
  output out_11
);

  or or_1 (out_9, D4, D5, D6, D7);
  or or_2 (out_10, D2, D3, D6, D7);
  or or_3 (out_11, D1, D3, D5, D7);

  // Notes on the sheet:
  //   Figure:Encoder
endmodule
