// Logisim project EncoderImplementation.circ as structural Verilog: 1 circuit, main circuit main
module main (
  input  D0,
  input  D1,
  input  D2,
  input  in_4,
  input  in_5,
  input  D5,
  input  in_7,
  input  D7,
  output out_9,
  output out_10,
  output out_11
);

  or or_1 (out_9, in_5, D5, in_7, D7);
  or or_2 (out_10, D2, in_4, in_7, D7);
  or or_3 (out_11, D1, in_4, D5, D7);

  // Notes on the sheet:
  //   Octal to Binary Encoder
  //   D3
  //   D4
  //   D6
  //   Y
  //   X
  //   Z
endmodule
