// Logisim project Excess-3CodeConverter.circ as structural Verilog
module Code_Converter (
  input  A,
  input  B,
  input  C,
  input  D,
  output W,
  output X,
  output Y,
  output Z
);

  wire and_1_out, and_2_out, and_3_out, and_4_out, and_5_out, and_6_out, and_7_out, and_8_out, and_9_out,
       not_1_out, not_2_out, not_3_out, not_4_out, not_5_out, not_6_out, not_7_out;

  and and_1 (and_1_out, B, D);
  and and_2 (and_2_out, B, C);
  not not_1 (not_1_out, B);
  and and_3 (and_3_out, not_1_out, D);
  not not_2 (not_2_out, B);
  and and_4 (and_4_out, not_2_out, C);
  and and_5 (and_5_out, B, not_3_out, not_4_out);
  not not_3 (not_3_out, C);
  not not_4 (not_4_out, D);
  and and_6 (and_6_out, A, B);
  not not_5 (not_5_out, C);
  and and_7 (and_7_out, not_5_out, not_6_out);
  not not_6 (not_6_out, D);
  and and_8 (and_8_out, C, D);
  not not_7 (not_7_out, D);
  and and_9 (and_9_out, A, B);
  or or_1 (W, and_1_out, and_2_out, A);
  or or_2 (X, and_3_out, and_4_out, and_5_out, and_6_out);
  or or_3 (Y, and_7_out, and_8_out);
  or or_4 (Z, not_7_out, and_9_out);
endmodule
