// Logisim project FullSubtractor.circ as structural Verilog: 1 circuit, main circuit main
module main (
  input  x,
  input  y,
  input  z,
  output Difference,
  output Borrow
);

  wire and_1_out, and_2_out, and_3_out, and_4_out, and_5_out, and_6_out, and_7_out, not_1_out, not_2_out,
       not_3_out, not_4_out, not_5_out, not_6_out, not_7_out, not_8_out;

  not not_1 (not_1_out, x);
  not not_2 (not_2_out, y);
  not not_3 (not_3_out, x);
  not not_4 (not_4_out, z);
  not not_5 (not_5_out, y);
  not not_6 (not_6_out, z);
  not not_7 (not_7_out, x);
  not not_8 (not_8_out, x);
  and and_1 (and_1_out, not_1_out, not_2_out, z);
  and and_2 (and_2_out, not_3_out, y, not_4_out);
  and and_3 (and_3_out, x, not_5_out, not_6_out);
  and and_4 (and_4_out, x, y, z);
  and and_5 (and_5_out, not_7_out, z);
  and and_6 (and_6_out, not_8_out, y);
  and and_7 (and_7_out, y, z);
  or or_1 (Difference, and_1_out, and_2_out, and_3_out, and_4_out);
  or or_2 (Borrow, and_5_out, and_6_out, and_7_out);

  // Notes on the sheet:
  //   Fig:Full Subtractor
endmodule
