// Logisim project HalfSubtractor.circ as structural Verilog: 1 circuit, main circuit main
module main (
  input  x,
  input  y,
  output Difference,
  output Borrow
);

  wire and_1_out, and_2_out, not_1_out, not_2_out, not_3_out;

  not not_1 (not_1_out, x);
  not not_2 (not_2_out, y);
  not not_3 (not_3_out, x);
  and and_1 (and_1_out, not_1_out, y);
  and and_2 (and_2_out, x, not_2_out);
  and and_3 (Borrow, not_3_out, y);
  or or_1 (Difference, and_1_out, and_2_out);
endmodule
