// Logisim project HighPriorityEncoder.circ as structural Verilog: 1 circuit, main circuit main
module main (
  input  D0,
  input  D1,
  input  D2,
  input  D3,
  output out_5,
  output out_6,
  output out_7
);

  wire and_1_out, not_1_out;

  not not_1 (not_1_out, D2);
  or or_1 (out_5, D0, D1, D2, D3);
  or or_2 (out_6, D2, D3);
  and and_1 (and_1_out, D1, not_1_out);
  or or_3 (out_7, and_1_out, D3);

  // Notes on the sheet:
  //   Figure:High Priority Encoder
  //   V
  //   X
  //   Y
endmodule
