// Logisim project JK flipflop.circ as structural Verilog: 1 circuit, main circuit main
module main (
  input  A,
  output out_2,
  output out_3,
  output out_4,
  output out_5
);

  wire and_1_out, and_2_out, and_3_out, and_4_out, and_5_out, and_6_out, and_7_out, and_8_out, and_9_out,
       and_10_out, and_11_out, and_12_out, and_13_out, clock_1_out, j_k_ff_1_qn, j_k_ff_2_qn, j_k_ff_3_qn,
       j_k_ff_4_qn, not_1_out, or_1_out, or_2_out, or_3_out, or_4_out, or_5_out, or_6_out, or_7_out,
       or_8_out, or_9_out, or_10_out, or_11_out, xor_1_out, xor_2_out, xor_3_out;

  J_K_Flip_Flop j_k_ff_1 (
    .J(and_9_out), .clk(clock_1_out), .K(1'b1), .Q(out_3), .Qn(j_k_ff_1_qn));  // open: preset, en, reset
  J_K_Flip_Flop j_k_ff_2 (
    .J(and_11_out), .clk(clock_1_out), .K(or_9_out), .Q(out_4), .Qn(j_k_ff_2_qn));  // open: preset, en, reset
  J_K_Flip_Flop j_k_ff_3 (
    .J(and_12_out), .clk(clock_1_out), .K(or_11_out), .Q(out_5), .Qn(j_k_ff_3_qn));  // open: preset, en, reset
  not not_1 (not_1_out, A);
  J_K_Flip_Flop j_k_ff_4 (
    .J(and_7_out), .clk(clock_1_out), .K(or_8_out), .Q(out_2), .Qn(j_k_ff_4_qn));  // open: preset, en, reset
  or or_1 (or_1_out, out_4, out_3);
  Clock clock_1 (.out(clock_1_out));
  xor xor_1 (xor_1_out, A, out_3);
  and and_1 (and_1_out, or_1_out, out_5);
  or or_2 (or_2_out, out_3, out_4);
  and and_2 (and_2_out, j_k_ff_3_qn, out_2);
  and and_3 (and_3_out, out_5, out_2);
  or or_3 (or_3_out, and_2_out, j_k_ff_4_qn, j_k_ff_2_qn);
  and and_4 (and_4_out, out_5, out_4);
  and and_5 (and_5_out, or_2_out, out_2);
  or or_4 (or_4_out, j_k_ff_4_qn, j_k_ff_3_qn);
  and and_6 (and_6_out, out_5, out_2);
  and and_7 (and_7_out, and_4_out, xor_1_out);
  or or_5 (or_5_out, and_3_out, out_3);
  and and_8 (and_8_out, out_3, out_4);
  or or_6 (or_6_out, out_3, out_4, out_2);
  or or_7 (or_7_out, out_3, A);
  and and_9 (and_9_out, or_3_out, not_1_out);
  and and_10 (and_10_out, or_5_out, A);
  xor xor_2 (xor_2_out, A, out_3);
  xor xor_3 (xor_3_out, A, out_3);
  or or_8 (or_8_out, and_1_out, and_10_out);
  and and_11 (and_11_out, or_4_out, xor_3_out);
  or or_9 (or_9_out, and_6_out, or_7_out);
  and and_12 (and_12_out, out_4, xor_2_out);
  and and_13 (and_13_out, or_6_out, A);
  or or_10 (or_10_out, and_5_out, and_8_out);
  or or_11 (or_11_out, or_10_out, and_13_out);

  // Notes on the sheet:
  //   JK-1
  //   JK-2
  //   JK-3
  //   JK-4
  //   Q1
  //   Q2
  //   Q3
  //   Q4
endmodule
