// Logisim project LowPriorityEncoder.circ as structural Verilog: 1 circuit, main circuit main
module main (
  input  D0,
  input  D1,
  input  D2,
  input  D3,
  output out_5,
  output out_6,
  output out_7
);

  wire and_2_out, and_3_out, not_1_out, not_2_out, not_3_out, not_4_out, not_5_out;

  not not_1 (not_1_out, D0);
  not not_2 (not_2_out, D1);
  not not_3 (not_3_out, D0);
  not not_4 (not_4_out, D0);
  and and_1 (out_5, not_1_out, not_2_out);
  or or_1 (out_6, D0, D1, D2, D3);
  not not_5 (not_5_out, D2);
  and and_2 (and_2_out, not_3_out, D1);
  and and_3 (and_3_out, not_4_out, not_5_out);
  or or_2 (out_7, and_2_out, and_3_out);

  // Notes on the sheet:
  //   V
  //   x
  //   Y
endmodule
