// Logisim project NANDGatesSevenSegmentOfBasicGates.circ as structural Verilog
module BasicGates (
  input  A,
  input  B,
  input  C,
  input  D
);

  wire and_1_out, and_2_out, and_3_out, and_4_out, and_5_out, and_6_out, and_7_out, and_8_out, and_9_out,
       and_10_out, and_11_out, and_12_out, and_13_out, and_14_out, and_15_out, and_16_out, and_17_out,
       and_18_out, and_19_out, and_20_out, and_21_out, and_22_out, and_23_out, and_24_out, and_25_out,
       and_26_out, and_27_out, and_28_out, and_29_out, and_30_out, and_31_out, not_1_out, not_2_out,
       not_3_out, not_4_out, not_5_out, not_6_out, not_7_out, not_8_out, not_9_out, not_10_out, not_11_out,
       not_12_out, not_13_out, not_14_out, not_15_out, not_16_out, not_17_out, not_18_out, not_19_out,
       not_20_out, not_21_out, not_22_out, not_23_out, not_24_out, not_25_out, not_26_out, not_27_out,
       not_28_out, not_29_out, not_30_out, not_31_out, not_32_out, not_33_out, not_34_out, not_35_out,
       not_36_out, not_37_out, not_38_out, not_39_out, not_40_out, not_41_out, not_42_out, not_43_out,
       not_44_out, not_45_out, not_46_out, not_47_out, not_48_out, not_49_out, not_50_out, not_51_out,
       not_52_out, not_53_out, or_1_out, or_2_out, or_3_out, or_4_out, or_5_out, or_6_out, or_7_out;

  not not_1 (not_1_out, A);
  and and_1 (and_1_out, not_1_out, not_2_out, not_3_out);
  not not_2 (not_2_out, B);
  not not_3 (not_3_out, C);
  not not_4 (not_4_out, A);
  and and_2 (and_2_out, not_4_out, not_5_out);
  not not_5 (not_5_out, D);
  and and_3 (and_3_out, A, not_6_out, D);
  not not_6 (not_6_out, B);
  and and_4 (and_4_out, A, B, not_7_out);
  not not_7 (not_7_out, C);
  not not_8 (not_8_out, A);
  and and_5 (and_5_out, not_8_out, not_9_out);
  not not_9 (not_9_out, B);
  not not_10 (not_10_out, B);
  and and_6 (and_6_out, not_10_out, not_11_out);
  not not_11 (not_11_out, C);
  not not_12 (not_12_out, B);
  and and_7 (and_7_out, not_12_out, not_13_out);
  not not_13 (not_13_out, D);
  not not_14 (not_14_out, A);
  not not_15 (not_15_out, C);
  and and_8 (and_8_out, not_14_out, not_15_out, D);
  not not_16 (not_16_out, A);
  and and_9 (and_9_out, not_16_out, C, not_17_out);
  not not_17 (not_17_out, D);
  not not_18 (not_18_out, C);
  and and_10 (and_10_out, A, not_18_out, not_19_out);
  not not_19 (not_19_out, D);
  not not_20 (not_20_out, B);
  and and_11 (and_11_out, not_20_out, not_21_out);
  not not_21 (not_21_out, D);
  not not_22 (not_22_out, B);
  and and_12 (and_12_out, not_22_out, C);
  and and_13 (and_13_out, B, not_23_out);
  not not_23 (not_23_out, C);
  and and_14 (and_14_out, A, not_24_out);
  not not_24 (not_24_out, B);
  not not_25 (not_25_out, A);
  and and_15 (and_15_out, not_25_out, not_26_out, not_27_out);
  not not_26 (not_26_out, B);
  not not_27 (not_27_out, C);
  not not_28 (not_28_out, A);
  and and_16 (and_16_out, not_28_out, not_29_out);
  not not_29 (not_29_out, D);
  and and_17 (and_17_out, A, not_30_out, D);
  not not_30 (not_30_out, B);
  and and_18 (and_18_out, A, B, not_31_out);
  not not_31 (not_31_out, C);
  not not_32 (not_32_out, A);
  not not_33 (not_33_out, B);
  not not_34 (not_34_out, C);
  not not_35 (not_35_out, A);
  not not_36 (not_36_out, D);
  not not_37 (not_37_out, A);
  not not_38 (not_38_out, D);
  not not_39 (not_39_out, C);
  not not_40 (not_40_out, A);
  not not_41 (not_41_out, B);
  not not_42 (not_42_out, D);
  not not_43 (not_43_out, A);
  not not_44 (not_44_out, C);
  not not_45 (not_45_out, C);
  not not_46 (not_46_out, B);
  not not_47 (not_47_out, A);
  and and_19 (and_19_out, not_47_out, not_48_out);
  not not_48 (not_48_out, C);
  not not_49 (not_49_out, A);
  and and_20 (and_20_out, not_49_out, B, not_50_out);
  not not_50 (not_50_out, D);
  and and_21 (and_21_out, B, not_51_out);
  not not_51 (not_51_out, C);
  not not_52 (not_52_out, B);
  and and_22 (and_22_out, A, not_52_out, D);
  not not_53 (not_53_out, A);
  or or_1 (or_1_out, and_1_out, and_2_out, and_3_out, and_4_out);
  or or_2 (or_2_out, and_11_out, and_12_out, and_13_out, and_14_out);
  or or_3 (or_3_out, and_15_out, and_16_out, and_17_out, and_18_out);
  and and_23 (and_23_out, not_32_out, not_33_out, not_34_out, D);
  and and_24 (and_24_out, not_35_out, C, not_36_out);
  and and_25 (and_25_out, not_37_out, B, not_38_out);
  and and_26 (and_26_out, A, B, not_39_out, D);
  and and_27 (and_27_out, not_40_out, not_41_out, C, not_42_out);
  and and_28 (and_28_out, not_43_out, B, not_44_out);
  and and_29 (and_29_out, B, not_45_out, D);
  and and_30 (and_30_out, A, not_46_out, C, D);
  or or_4 (or_4_out, and_19_out, and_20_out, and_21_out, and_22_out);
  and and_31 (and_31_out, not_53_out, B, C, D);
  or or_5 (or_5_out, and_5_out, and_6_out, and_7_out, and_8_out, and_9_out, and_10_out);
  or or_6 (or_6_out, and_23_out, and_24_out, and_25_out, and_26_out);
  or or_7 (or_7_out, and_27_out, and_28_out, and_29_out, and_30_out);
  _7_Segment_Display u_7_segment_display_1 (
    .g(or_4_out), .f(or_7_out), .a(or_1_out), .b(or_5_out), .e(or_6_out), .d(or_3_out), .c(or_2_out),
    .dp(and_31_out));

  // Notes on the sheet:
  //   a
  //   b
  //   c
  //   d
  //   e
  //   f
  //   g
endmodule

module NANDGatesSevenSegment (
  input  A,
  input  B,
  input  C,
  input  D
);

  wire nand_1_out, nand_2_out, nand_3_out, nand_4_out, nand_5_out, nand_6_out, nand_7_out, nand_8_out,
       nand_9_out, nand_10_out, nand_11_out, nand_12_out, nand_13_out, nand_14_out, nand_15_out, nand_16_out,
       nand_17_out, nand_18_out, nand_19_out, nand_20_out, nand_21_out, nand_22_out, nand_23_out,
       nand_24_out, nand_25_out, nand_26_out, nand_27_out, nand_28_out, nand_29_out, nand_30_out,
       nand_31_out, nand_32_out, nand_33_out, nand_34_out, nand_35_out, nand_36_out, nand_37_out,
       nand_38_out, nand_39_out, nand_40_out, nand_41_out, nand_42_out, nand_43_out, nand_44_out,
       nand_45_out, nand_46_out, nand_47_out, nand_48_out, nand_49_out, nand_50_out, nand_51_out,
       nand_52_out, nand_53_out, nand_54_out, nand_55_out, nand_56_out, nand_57_out, nand_58_out,
       nand_59_out, nand_60_out, nand_61_out, nand_62_out, nand_63_out, nand_64_out, nand_65_out,
       nand_66_out, nand_67_out, nand_68_out, nand_69_out, nand_70_out, nand_71_out, nand_72_out,
       nand_73_out, nand_74_out, nand_75_out, nand_76_out, nand_77_out, nand_78_out, nand_79_out,
       nand_80_out, nand_81_out, nand_82_out, nand_83_out, nand_84_out, nand_85_out, nand_86_out,
       nand_87_out, nand_88_out, nand_89_out, nand_90_out, nand_91_out, nand_92_out;

  nand nand_1 (nand_1_out, A, A);
  nand nand_2 (nand_2_out, B, B);
  nand nand_3 (nand_3_out, C, C);
  nand nand_4 (nand_4_out, A, A);
  nand nand_5 (nand_5_out, D, D);
  nand nand_6 (nand_6_out, B, B);
  nand nand_7 (nand_7_out, C, C);
  nand nand_8 (nand_8_out, A, A);
  nand nand_9 (nand_9_out, B, B);
  nand nand_10 (nand_10_out, B, B);
  nand nand_11 (nand_11_out, C, C);
  nand nand_12 (nand_12_out, B, B);
  nand nand_13 (nand_13_out, D, D);
  nand nand_14 (nand_14_out, A, A);
  nand nand_15 (nand_15_out, C, C);
  nand nand_16 (nand_16_out, A, A);
  nand nand_17 (nand_17_out, D, D);
  nand nand_18 (nand_18_out, C, C);
  nand nand_19 (nand_19_out, D, D);
  nand nand_20 (nand_20_out, B, B);
  nand nand_21 (nand_21_out, D, D);
  nand nand_22 (nand_22_out, B, B);
  nand nand_23 (nand_23_out, C, C);
  nand nand_24 (nand_24_out, B, B);
  nand nand_25 (nand_25_out, A, A);
  nand nand_26 (nand_26_out, B, B);
  nand nand_27 (nand_27_out, C, C);
  nand nand_28 (nand_28_out, A, A);
  nand nand_29 (nand_29_out, D, D);
  nand nand_30 (nand_30_out, B, B);
  nand nand_31 (nand_31_out, C, C);
  nand nand_32 (nand_32_out, A, A);
  nand nand_33 (nand_33_out, B, B);
  nand nand_34 (nand_34_out, C, C);
  nand nand_35 (nand_35_out, A, A);
  nand nand_36 (nand_36_out, D, D);
  nand nand_37 (nand_37_out, A, A);
  nand nand_38 (nand_38_out, D, D);
  nand nand_39 (nand_39_out, C, C);
  nand nand_40 (nand_40_out, A, A);
  nand nand_41 (nand_41_out, B, B);
  nand nand_42 (nand_42_out, D, D);
  nand nand_43 (nand_43_out, A, A);
  nand nand_44 (nand_44_out, C, C);
  nand nand_45 (nand_45_out, C, C);
  nand nand_46 (nand_46_out, B, B);
  nand nand_47 (nand_47_out, A, A);
  nand nand_48 (nand_48_out, C, C);
  nand nand_49 (nand_49_out, A, A);
  nand nand_50 (nand_50_out, D, D);
  nand nand_51 (nand_51_out, C, C);
  nand nand_52 (nand_52_out, B, B);
  nand nand_53 (nand_53_out, A, A);
  nand nand_54 (nand_54_out, nand_1_out, nand_2_out, nand_3_out);
  nand nand_55 (nand_55_out, nand_4_out, nand_5_out);
  nand nand_56 (nand_56_out, A, nand_6_out, D);
  nand nand_57 (nand_57_out, A, B, nand_7_out);
  nand nand_58 (nand_58_out, nand_8_out, nand_9_out);
  nand nand_59 (nand_59_out, nand_10_out, nand_11_out);
  nand nand_60 (nand_60_out, nand_12_out, nand_13_out);
  nand nand_61 (nand_61_out, nand_14_out, nand_15_out, D);
  nand nand_62 (nand_62_out, nand_16_out, C, nand_17_out);
  nand nand_63 (nand_63_out, A, nand_18_out, nand_19_out);
  nand nand_64 (nand_64_out, nand_20_out, nand_21_out);
  nand nand_65 (nand_65_out, nand_22_out, C);
  nand nand_66 (nand_66_out, B, nand_23_out);
  nand nand_67 (nand_67_out, A, nand_24_out);
  nand nand_68 (nand_68_out, nand_25_out, nand_26_out, nand_27_out);
  nand nand_69 (nand_69_out, nand_28_out, nand_29_out);
  nand nand_70 (nand_70_out, A, nand_30_out, D);
  nand nand_71 (nand_71_out, A, B, nand_31_out);
  nand nand_72 (nand_72_out, nand_32_out, nand_33_out, nand_34_out, D);
  nand nand_73 (nand_73_out, nand_35_out, C, nand_36_out);
  nand nand_74 (nand_74_out, nand_37_out, B, nand_38_out);
  nand nand_75 (nand_75_out, A, B, nand_39_out, D);
  nand nand_76 (nand_76_out, nand_40_out, nand_41_out, C, nand_42_out);
  nand nand_77 (nand_77_out, nand_43_out, B, nand_44_out);
  nand nand_78 (nand_78_out, B, nand_45_out, D);
  nand nand_79 (nand_79_out, A, nand_46_out, C, D);
  nand nand_80 (nand_80_out, nand_47_out, nand_48_out);
  nand nand_81 (nand_81_out, nand_49_out, B, nand_50_out);
  nand nand_82 (nand_82_out, B, nand_51_out);
  nand nand_83 (nand_83_out, A, nand_52_out, D);
  nand nand_84 (nand_84_out, nand_53_out, B, C, D);
  nand nand_85 (nand_85_out, nand_54_out, nand_55_out, nand_56_out, nand_57_out);
  nand nand_86 (nand_86_out, nand_58_out, nand_59_out, nand_60_out, nand_61_out, nand_62_out, nand_63_out);
  nand nand_87 (nand_87_out, nand_64_out, nand_65_out, nand_66_out, nand_67_out);
  nand nand_88 (nand_88_out, nand_68_out, nand_69_out, nand_70_out, nand_71_out);
  nand nand_89 (nand_89_out, nand_72_out, nand_73_out, nand_74_out, nand_75_out);
  nand nand_90 (nand_90_out, nand_76_out, nand_77_out, nand_78_out, nand_79_out);
  nand nand_91 (nand_91_out, nand_80_out, nand_81_out, nand_82_out, nand_83_out);
  nand nand_92 (nand_92_out, nand_84_out, nand_84_out);
  _7_Segment_Display u_7_segment_display_1 (
    .g(nand_91_out), .f(nand_90_out), .a(nand_85_out), .b(nand_86_out), .e(nand_89_out), .d(nand_88_out),
    .c(nand_87_out), .dp(nand_92_out));

  // Notes on the sheet:
  //   a
  //   b
  //   c
  //   d
  //   g
  //   dot
endmodule
