// Logisim project PISO REgister.circ as structural Verilog: 1 circuit, main circuit main
module main (
  input  SHIFT,
  input  B2,
  input  B1,
  input  B0,
  input  in_5,
  output SERIAL_OUTPUT
);

  wire and_1_out, and_2_out, and_3_out, and_4_out, and_5_out, and_6_out, clock_1_out, d_ff_1_q, d_ff_2_q,
       d_ff_3_q, not_1_out, or_1_out, or_2_out, or_3_out;

  not not_1 (not_1_out, SHIFT);
  and and_1 (and_1_out, not_1_out, B0);
  and and_2 (and_2_out, SHIFT, d_ff_1_q);
  and and_3 (and_3_out, B1, not_1_out);
  and and_4 (and_4_out, d_ff_2_q, SHIFT);
  buf and_5 (and_5_out, d_ff_3_q);  // AND_Gate
  and and_6 (and_6_out, not_1_out, B2);
  Clock clock_1 (.out(clock_1_out));
  or or_1 (or_1_out, and_1_out, and_2_out);
  or or_2 (or_2_out, and_3_out, and_4_out);
  or or_3 (or_3_out, and_6_out, and_5_out);
  D_Flip_Flop d_ff_1 (.clk(clock_1_out), .D(in_5), .Q(d_ff_1_q));  // open: Qn, preset, en, reset
  D_Flip_Flop d_ff_2 (.clk(clock_1_out), .D(or_1_out), .Q(d_ff_2_q));  // open: Qn, preset, en, reset
  D_Flip_Flop d_ff_3 (.clk(clock_1_out), .D(or_2_out), .Q(d_ff_3_q));  // open: Qn, preset, en, reset
  D_Flip_Flop d_ff_4 (.clk(clock_1_out), .D(or_3_out), .Q(SERIAL_OUTPUT));  // open: Qn, preset, en, reset

  // Notes on the sheet:
  //   PArallel
  //   Inputs
  //   LOAD
  //   B3
  //   Fig:PiSO Register
endmodule
