// Logisim project Register File.circ as structural Verilog: 1 circuit, main circuit main
module main (
  input  [3:0] in_1,
  input  [1:0] in_2,
  input  [1:0] RD,
  input  [1:0] in_4,
  output [3:0] Data_of_rs,
  output [3:0] Data_of_rt
);

  wire clock_1_out, decoder_1_out0, decoder_1_out1, decoder_1_out2, decoder_1_out3, undriven;
  wire [3:0] register_1_q, register_2_q, register_3_q, register_4_q;

  Decoder #(.select(2)) decoder_1 (
    .out0(decoder_1_out0), .out1(decoder_1_out1), .out2(decoder_1_out2), .out3(decoder_1_out3), .sel(RD),
    .en(undriven));
  Clock clock_1 (.out(clock_1_out));
  Register #(.width(4)) register_1 (.D(in_1), .en(decoder_1_out0), .Q(register_1_q), .clk(clock_1_out));  // open: clr
  Register #(.width(4)) register_2 (.D(in_1), .en(decoder_1_out1), .Q(register_2_q), .clk(clock_1_out));  // open: clr
  Register #(.width(4)) register_3 (.D(in_1), .en(decoder_1_out2), .Q(register_3_q), .clk(clock_1_out));  // open: clr
  Register #(.width(4)) register_4 (.D(in_1), .en(decoder_1_out3), .Q(register_4_q), .clk(clock_1_out));  // open: clr
  Multiplexer #(.select(2), .width(4)) multiplexer_1 (
    .in0(register_1_q), .in1(register_2_q), .in2(register_3_q), .in3(register_4_q), .out(Data_of_rs),
    .sel(in_2));  // open: en
  Multiplexer #(.select(2), .width(4)) multiplexer_2 (
    .in0(register_1_q), .in1(register_2_q), .in2(register_3_q), .in3(register_4_q), .out(Data_of_rt),
    .sel(in_4));  // open: en

  // Notes on the sheet:
  //   (rd)
  //   Write Data
  //   Register number
  //   Register Number
  //   (rt)
  //   (rs)
endmodule
