// Logisim project RegisterFile.circ as structural Verilog: 2 circuits, main circuit main
module main (
  input  [15:0] WriteData,
  input  WriteSig,
  input  [2:0] WriteReg,
  input  [2:0] ReadReg1,
  input  [2:0] ReadReg2,
  output [15:0] ReadData1,
  output [15:0] ReadData2
);

  _8Registers u_8registers_1 (
    .in_2(WriteData), .WriteSignal(WriteSig), .WriteRegNo(WriteReg), .ReadRegNo_1(ReadReg1),
    .ReadRegNo_2(ReadReg2), .ReadData1(ReadData1), .Readdata2(ReadData2));  // open: WriteData
endmodule

module _8Registers (
  input  [15:0] WriteData,
  input  [15:0] in_2,
  input  WriteSignal,
  input  [2:0] WriteRegNo,
  input  [2:0] ReadRegNo_1,
  input  [2:0] ReadRegNo_2,
  output [15:0] ReadData1,
  output [15:0] Readdata2
);

  wire and_1_out, and_2_out, and_3_out, and_4_out, and_5_out, and_6_out, and_7_out, and_8_out, CLK_out,
       decoder_1_out0, decoder_1_out1, decoder_1_out2, decoder_1_out3, decoder_1_out4, decoder_1_out5,
       decoder_1_out6, decoder_1_out7;
  wire [15:0] _0_q, s0_q, s1_q, s2_q, s3_q, sp_q, t0_q, t1_q;

  Decoder #(.select(3)) decoder_1 (
    .out0(decoder_1_out0), .out1(decoder_1_out1), .out2(decoder_1_out2), .out3(decoder_1_out3),
    .out4(decoder_1_out4), .out5(decoder_1_out5), .out6(decoder_1_out6), .out7(decoder_1_out7),
    .sel(WriteRegNo));  // open: en
  and and_1 (and_1_out, decoder_1_out0, WriteSignal);
  and and_2 (and_2_out, decoder_1_out1, WriteSignal);
  and and_3 (and_3_out, decoder_1_out2, WriteSignal);
  and and_4 (and_4_out, decoder_1_out3, WriteSignal);
  and and_5 (and_5_out, decoder_1_out4, WriteSignal);
  and and_6 (and_6_out, decoder_1_out5, WriteSignal);
  and and_7 (and_7_out, decoder_1_out6, WriteSignal);
  and and_8 (and_8_out, decoder_1_out7, WriteSignal);
  Clock CLK (.out(CLK_out));
  Register #(.width(16)) _0 (.D(in_2), .en(and_1_out), .Q(_0_q), .clk(CLK_out));  // open: clr
  Register #(.width(16)) sp (.D(WriteData), .en(and_2_out), .Q(sp_q), .clk(CLK_out));  // open: clr
  Register #(.width(16)) s0 (.D(WriteData), .en(and_3_out), .Q(s0_q), .clk(CLK_out));  // open: clr
  Register #(.width(16)) s1 (.D(WriteData), .en(and_4_out), .Q(s1_q), .clk(CLK_out));  // open: clr
  Register #(.width(16)) s2 (.D(WriteData), .en(and_5_out), .Q(s2_q), .clk(CLK_out));  // open: clr
  Register #(.width(16)) s3 (.D(WriteData), .en(and_6_out), .Q(s3_q), .clk(CLK_out));  // open: clr
  Register #(.width(16)) t0 (.D(WriteData), .en(and_7_out), .Q(t0_q), .clk(CLK_out));  // open: clr
  Register #(.width(16)) t1 (.D(WriteData), .en(and_8_out), .Q(t1_q), .clk(CLK_out));  // open: clr
  Multiplexer #(.select(3), .width(16)) multiplexer_1 (
    .in0(_0_q), .in1(sp_q), .in2(s0_q), .in3(s1_q), .in4(s2_q), .in5(s3_q), .in6(t0_q), .in7(t1_q),
    .out(ReadData1), .sel(ReadRegNo_1));  // open: en
  Multiplexer #(.select(3), .width(16)) multiplexer_2 (
    .in0(_0_q), .in1(sp_q), .in2(s0_q), .in3(s1_q), .in4(s2_q), .in5(s3_q), .in6(t0_q), .in7(t1_q),
    .out(Readdata2), .sel(ReadRegNo_2));  // open: en
endmodule
