// Logisim project SevenSegment7basicGates.circ as structural Verilog
module SevenSegment3 (
  input  A,
  input  B,
  input  C,
  input  D,
  output h
);

  wire and_1_out, and_2_out, and_3_out, and_4_out, and_5_out, and_6_out, and_7_out, and_8_out, and_9_out,
       and_10_out, and_11_out, and_12_out, and_13_out, and_14_out, and_15_out, and_16_out, and_17_out,
       and_18_out, and_19_out, and_20_out, and_21_out, and_22_out, and_23_out, and_24_out, and_25_out,
       and_26_out, and_27_out, and_28_out, and_29_out, and_30_out, not_1_out, not_2_out, not_3_out,
       not_4_out, not_5_out, not_6_out, not_7_out, not_8_out, not_9_out, not_10_out, not_11_out, not_12_out,
       not_13_out, not_14_out, not_15_out, not_16_out, not_17_out, not_18_out, not_19_out, not_20_out,
       not_21_out, not_22_out, not_23_out, not_24_out, not_25_out, not_26_out, not_27_out, not_28_out,
       not_29_out, not_30_out, not_31_out, not_32_out, not_33_out, not_34_out, not_35_out, not_36_out,
       not_37_out, not_38_out, not_39_out, not_40_out, not_41_out, not_42_out, not_43_out, not_44_out,
       not_45_out, not_46_out, not_47_out, not_48_out, not_49_out, not_50_out, not_51_out, not_52_out,
       or_1_out, or_2_out, or_3_out, or_4_out, or_5_out, or_6_out, or_7_out;

  not not_1 (not_1_out, A);
  not not_2 (not_2_out, B);
  and and_1 (and_1_out, not_1_out, not_2_out, not_3_out);
  not not_3 (not_3_out, C);
  not not_4 (not_4_out, A);
  and and_2 (and_2_out, not_4_out, not_5_out);
  not not_5 (not_5_out, D);
  and and_3 (and_3_out, A, not_6_out, D);
  not not_6 (not_6_out, B);
  and and_4 (and_4_out, A, B, not_7_out);
  not not_7 (not_7_out, C);
  not not_8 (not_8_out, A);
  and and_5 (and_5_out, not_8_out, not_9_out);
  not not_9 (not_9_out, B);
  not not_10 (not_10_out, B);
  and and_6 (and_6_out, not_10_out, not_11_out);
  not not_11 (not_11_out, C);
  not not_12 (not_12_out, B);
  and and_7 (and_7_out, not_12_out, not_13_out);
  not not_13 (not_13_out, D);
  not not_14 (not_14_out, A);
  and and_8 (and_8_out, not_14_out, not_15_out, D);
  not not_15 (not_15_out, C);
  not not_16 (not_16_out, A);
  and and_9 (and_9_out, not_16_out, C, not_17_out);
  not not_17 (not_17_out, D);
  not not_18 (not_18_out, C);
  and and_10 (and_10_out, A, not_18_out, not_19_out);
  not not_19 (not_19_out, D);
  not not_20 (not_20_out, B);
  and and_11 (and_11_out, not_20_out, not_21_out);
  not not_21 (not_21_out, D);
  not not_22 (not_22_out, B);
  and and_12 (and_12_out, not_22_out, C);
  and and_13 (and_13_out, B, not_23_out);
  not not_23 (not_23_out, C);
  and and_14 (and_14_out, A, not_24_out);
  not not_24 (not_24_out, B);
  not not_25 (not_25_out, A);
  and and_15 (and_15_out, not_25_out, not_26_out, not_27_out);
  not not_26 (not_26_out, B);
  not not_27 (not_27_out, C);
  not not_28 (not_28_out, A);
  and and_16 (and_16_out, not_28_out, not_29_out);
  not not_29 (not_29_out, D);
  and and_17 (and_17_out, A, not_30_out, D);
  not not_30 (not_30_out, B);
  and and_18 (and_18_out, A, B, not_31_out);
  not not_31 (not_31_out, C);
  not not_32 (not_32_out, A);
  not not_33 (not_33_out, B);
  not not_34 (not_34_out, C);
  not not_35 (not_35_out, A);
  not not_36 (not_36_out, D);
  not not_37 (not_37_out, A);
  not not_38 (not_38_out, D);
  not not_39 (not_39_out, C);
  not not_40 (not_40_out, A);
  not not_41 (not_41_out, B);
  not not_42 (not_42_out, D);
  not not_43 (not_43_out, A);
  not not_44 (not_44_out, C);
  not not_45 (not_45_out, C);
  not not_46 (not_46_out, B);
  not not_47 (not_47_out, A);
  and and_19 (and_19_out, not_47_out, not_48_out);
  not not_48 (not_48_out, C);
  not not_49 (not_49_out, A);
  and and_20 (and_20_out, not_49_out, B, not_50_out);
  not not_50 (not_50_out, D);
  and and_21 (and_21_out, B, not_51_out);
  not not_51 (not_51_out, C);
  not not_52 (not_52_out, B);
  and and_22 (and_22_out, A, not_52_out, D);
  or or_1 (or_1_out, and_1_out, and_2_out, and_3_out, and_4_out);
  or or_2 (or_2_out, and_11_out, and_12_out, and_13_out, and_14_out);
  or or_3 (or_3_out, and_15_out, and_16_out, and_17_out, and_18_out);
  and and_23 (and_23_out, not_32_out, not_33_out, not_34_out, D);
  and and_24 (and_24_out, not_35_out, C, not_36_out);
  and and_25 (and_25_out, not_37_out, B, not_38_out);
  and and_26 (and_26_out, A, B, not_39_out, D);
  and and_27 (and_27_out, not_40_out, not_41_out, C, not_42_out);
  and and_28 (and_28_out, not_43_out, B, not_44_out);
  and and_29 (and_29_out, B, not_45_out, D);
  and and_30 (and_30_out, A, not_46_out, C, D);
  or or_4 (or_4_out, and_19_out, and_20_out, and_21_out, and_22_out);
  or or_5 (or_5_out, and_5_out, and_6_out, and_7_out, and_8_out, and_9_out, and_10_out);
  or or_6 (or_6_out, and_23_out, and_24_out, and_25_out, and_26_out);
  or or_7 (or_7_out, and_27_out, and_28_out, and_29_out, and_30_out);

  assign h = 1'b0;
endmodule

module SevenSegment7 (
  input  A,
  input  B,
  input  C,
  input  D
);

  wire and_1_out, and_2_out, and_3_out, and_4_out, and_5_out, and_6_out, and_7_out, and_8_out, and_9_out,
       and_10_out, and_11_out, and_12_out, and_13_out, and_14_out, and_15_out, and_16_out, and_17_out,
       and_18_out, and_19_out, and_20_out, and_21_out, and_22_out, and_23_out, and_24_out, and_25_out,
       and_26_out, and_27_out, and_28_out, and_29_out, and_30_out, and_31_out, not_1_out, not_2_out,
       not_3_out, not_4_out, not_5_out, not_6_out, not_7_out, not_8_out, not_9_out, not_10_out, not_11_out,
       not_12_out, not_13_out, not_14_out, not_15_out, not_16_out, not_17_out, not_18_out, not_19_out,
       not_20_out, not_21_out, not_22_out, not_23_out, not_24_out, not_25_out, not_26_out, not_27_out,
       not_28_out, not_29_out, not_30_out, not_31_out, not_32_out, not_33_out, not_34_out, not_35_out,
       not_36_out, not_37_out, not_38_out, not_39_out, not_40_out, not_41_out, not_42_out, not_43_out,
       not_44_out, not_45_out, not_46_out, not_47_out, not_48_out, not_49_out, not_50_out, not_51_out,
       not_52_out, not_53_out, or_1_out, or_2_out, or_3_out, or_4_out, or_5_out, or_6_out, or_7_out;

  not not_1 (not_1_out, A);
  and and_1 (and_1_out, not_1_out, not_2_out, not_3_out);
  not not_2 (not_2_out, B);
  not not_3 (not_3_out, C);
  not not_4 (not_4_out, A);
  and and_2 (and_2_out, not_4_out, not_5_out);
  not not_5 (not_5_out, D);
  and and_3 (and_3_out, A, not_6_out, D);
  not not_6 (not_6_out, B);
  and and_4 (and_4_out, A, B, not_7_out);
  not not_7 (not_7_out, C);
  not not_8 (not_8_out, A);
  and and_5 (and_5_out, not_8_out, not_9_out);
  not not_9 (not_9_out, B);
  not not_10 (not_10_out, B);
  and and_6 (and_6_out, not_10_out, not_11_out);
  not not_11 (not_11_out, C);
  not not_12 (not_12_out, B);
  and and_7 (and_7_out, not_12_out, not_13_out);
  not not_13 (not_13_out, D);
  not not_14 (not_14_out, A);
  and and_8 (and_8_out, not_14_out, not_15_out, D);
  not not_15 (not_15_out, C);
  not not_16 (not_16_out, A);
  and and_9 (and_9_out, not_16_out, C, not_17_out);
  not not_17 (not_17_out, D);
  and and_10 (and_10_out, A, not_18_out, not_19_out);
  not not_18 (not_18_out, C);
  not not_19 (not_19_out, D);
  not not_20 (not_20_out, B);
  and and_11 (and_11_out, not_20_out, not_21_out);
  not not_21 (not_21_out, D);
  not not_22 (not_22_out, B);
  and and_12 (and_12_out, not_22_out, C);
  and and_13 (and_13_out, B, not_23_out);
  not not_23 (not_23_out, C);
  and and_14 (and_14_out, A, not_24_out);
  not not_24 (not_24_out, B);
  not not_25 (not_25_out, A);
  and and_15 (and_15_out, not_25_out, not_26_out, not_27_out);
  not not_26 (not_26_out, B);
  not not_27 (not_27_out, C);
  not not_28 (not_28_out, A);
  and and_16 (and_16_out, not_28_out, not_29_out);
  not not_29 (not_29_out, D);
  and and_17 (and_17_out, A, not_30_out, D);
  not not_30 (not_30_out, B);
  and and_18 (and_18_out, A, B, not_31_out);
  not not_31 (not_31_out, C);
  not not_32 (not_32_out, A);
  not not_33 (not_33_out, B);
  not not_34 (not_34_out, C);
  not not_35 (not_35_out, A);
  not not_36 (not_36_out, D);
  not not_37 (not_37_out, A);
  not not_38 (not_38_out, D);
  not not_39 (not_39_out, C);
  not not_40 (not_40_out, A);
  not not_41 (not_41_out, B);
  not not_42 (not_42_out, D);
  not not_43 (not_43_out, A);
  not not_44 (not_44_out, C);
  not not_45 (not_45_out, C);
  not not_46 (not_46_out, B);
  not not_47 (not_47_out, A);
  and and_19 (and_19_out, not_47_out, not_48_out);
  not not_48 (not_48_out, C);
  not not_49 (not_49_out, A);
  and and_20 (and_20_out, not_49_out, B, not_50_out);
  not not_50 (not_50_out, D);
  and and_21 (and_21_out, B, not_51_out);
  not not_51 (not_51_out, C);
  and and_22 (and_22_out, A, not_52_out, D);
  not not_52 (not_52_out, B);
  not not_53 (not_53_out, A);
  or or_1 (or_1_out, and_1_out, and_2_out, and_3_out, and_4_out);
  or or_2 (or_2_out, and_11_out, and_12_out, and_13_out, and_14_out);
  or or_3 (or_3_out, and_15_out, and_16_out, and_17_out, and_18_out);
  and and_23 (and_23_out, not_32_out, not_33_out, not_34_out, D);
  and and_24 (and_24_out, not_35_out, C, not_36_out);
  and and_25 (and_25_out, not_37_out, B, not_38_out);
  and and_26 (and_26_out, A, B, not_39_out, D);
  and and_27 (and_27_out, not_40_out, not_41_out, C, not_42_out);
  and and_28 (and_28_out, not_43_out, B, not_44_out);
  and and_29 (and_29_out, B, not_45_out, D);
  and and_30 (and_30_out, A, not_46_out, C, D);
  or or_4 (or_4_out, and_19_out, and_20_out, and_21_out, and_22_out);
  and and_31 (and_31_out, not_53_out, B, C, D);
  or or_5 (or_5_out, and_5_out, and_6_out, and_7_out, and_8_out, and_9_out, and_10_out);
  or or_6 (or_6_out, and_23_out, and_24_out, and_25_out, and_26_out);
  or or_7 (or_7_out, and_27_out, and_28_out, and_29_out, and_30_out);
  _7_Segment_Display u_7_segment_display_1 (
    .g(or_4_out), .f(or_7_out), .a(or_1_out), .b(or_5_out), .e(or_6_out), .d(or_3_out), .c(or_2_out),
    .dp(and_31_out));

  // Notes on the sheet:
  //   c
  //   d
  //   h
  //   a
  //   b
  //   e
  //   f
  //   g
endmodule
