// Logisim project SevenSegmentDisplay.circ as structural Verilog: 1 circuit, main circuit main
module main (
  input  A,
  input  D,
  input  B,
  input  in_4,
  input  C,
  input  B_2,
  input  C_2,
  input  A_2,
  input  D_2,
  output out_10
);

  wire and_1_out, and_2_out, and_3_out, and_4_out, and_5_out, and_6_out, and_7_out, and_9_out, and_10_out,
       not_1_out, not_2_out, not_3_out, not_5_out, not_6_out, or_1_out;

  not not_1 (not_1_out, A);
  not not_2 (not_2_out, D);
  not not_3 (not_3_out, B);
  not not_4 (not_2_out, C);
  not not_5 (not_5_out, B);
  and and_1 (and_1_out, not_1_out, not_2_out);
  and and_2 (and_2_out, A, D, not_3_out);
  and and_3 (and_3_out, A, B, not_2_out);
  not not_6 (not_6_out, B_2);
  not not_7 (not_6_out, A_2);
  not not_8 (not_6_out, A_2);
  not not_9 (not_6_out, D_2);
  and and_4 (and_4_out, not_2_out, not_5_out, not_2_out);
  and and_5 (and_5_out, not_6_out, not_6_out);
  and and_6 (and_6_out, not_6_out, not_6_out, not_6_out);
  and and_7 (and_7_out, A_2, not_6_out, not_6_out);
  and and_8 (and_7_out, not_6_out, D_2, not_6_out);
  and and_9 (and_9_out, not_6_out, not_6_out);
  and and_10 (and_10_out, not_6_out, not_6_out, A_2);
  or or_1 (or_1_out, and_1_out, and_2_out, and_3_out, and_4_out);
  or or_2 (out_10, and_5_out, and_6_out, and_7_out, and_7_out, and_10_out, and_9_out);

  assign C_2 = A_2;

  // Notes on the sheet:
  //   a
endmodule
