// Logisim project UniversalGate01.circ as structural Verilog: 1 circuit, main circuit main
module main (
  input  A,
  input  C,
  input  in_3,
  output out_4
);

  wire nand_1_out, nand_2_out, nand_3_out;

  nand nand_1 (nand_1_out, A, in_3);
  nand nand_2 (nand_2_out, in_3, in_3);
  nand nand_3 (nand_3_out, C, nand_2_out);
  nand nand_4 (out_4, nand_1_out, nand_3_out);

  // Notes on the sheet:
  //   B
  //   Figure:NAND GATE IMPLEMENTATION
  //   ID#1813153642
endmodule
