// Logisim project UpDownCounter2.circ as structural Verilog
module UpDownCounter (
  input  M,
  input  A,
  input  B,
  input  C,
  output T1,
  output T2,
  output T3
);

  wire and_1_out, and_2_out, and_3_out, and_4_out, not_1_out, not_2_out, not_3_out, not_4_out, not_5_out;

  not not_1 (not_1_out, M);
  not not_2 (not_2_out, B);
  and and_1 (and_1_out, not_1_out, not_2_out, not_3_out);
  not not_3 (not_3_out, C);
  and and_2 (and_2_out, M, B, C);
  not not_4 (not_4_out, M);
  and and_3 (and_3_out, not_4_out, not_5_out);
  not not_5 (not_5_out, C);
  and and_4 (and_4_out, M, C);
  or or_1 (T1, and_1_out, and_2_out);
  or or_2 (T2, and_3_out, and_4_out);

  assign T3 = 1'b1;
endmodule
