// Logisim project UpDownCounterCorrect.circ as structural Verilog: 1 circuit, main circuit main
module main (
  input  M,
  output [2:0] Output
);

  wire and_1_out, and_2_out, B_qn, C_qn, clock_1_out, not_1_out, or_1_out, xnor_1_out;

  not not_1 (not_1_out, M);
  xnor xnor_1 (xnor_1_out, M, Output[0]);
  and and_1 (and_1_out, M, Output[1], Output[0]);
  and and_2 (and_2_out, C_qn, B_qn, not_1_out);
  Clock clock_1 (.out(clock_1_out));
  or or_1 (or_1_out, and_2_out, and_1_out);
  T_Flip_Flop A (.clk(clock_1_out), .T(or_1_out), .Q(Output[2]));  // open: Qn, preset, reset, en
  T_Flip_Flop B (.clk(clock_1_out), .T(xnor_1_out), .Q(Output[1]), .Qn(B_qn));  // open: preset, reset, en
  T_Flip_Flop C (.clk(clock_1_out), .T(1'b1), .Q(Output[0]), .Qn(C_qn));  // open: preset, reset, en
endmodule
