// Logisim project datapath.circ as structural Verilog: 1 circuit, main circuit main
module main (
  input  in_1,
  input  [7:0] in_2,
  input  Carry_In,
  input  Binvert,
  output [1:0] out_5,
  output [1:0] out_6,
  output [1:0] out_7,
  output [1:0] out_8,
  output [1:0] Result,
  output Carry_1,
  output [1:0] out_11,
  output [1:0] out_12
);

  wire Clock_out;
  wire [7:0] adder_1_out, register_1_q;

  Register register_1 (.D(adder_1_out), .Q(register_1_q), .clk(Clock_out));  // open: en, clr
  Adder adder_1 (.a(in_2), .b(register_1_q), .out(adder_1_out), .cin(in_1));  // open: cout
  ROM rom_1 (.addr(register_1_q), .data({out_12, out_8, out_7, out_6}));  // open: sel
  Clock Clock (.out(Clock_out));
  Register_File register_file_1 (
    .Data_IN(Result), .Data01(out_5), .Data02(out_11), .Data_Address(out_8), .clk(Clock_out), .RS(out_6),
    .RT(out_7));
  // ALU_2_bit alu_2_bit_1: pin names not known; wires that end beside it: out_5, out_11, out_12, Binvert, Carry_In, Result, Carry_1

  // Notes on the sheet:
  //   contents of rom_1 (hex, n*v repeats v):
  //   9b 9b b9 b9 c6
endmodule
