// Logisim project decoder 3 bit.circ as structural Verilog
module dECODER (
  input  x,
  input  y,
  input  z,
  output D0,
  output D1,
  output D2,
  output D3,
  output D4,
  output D5,
  output D6,
  output D7
);

  wire not_1_out, not_2_out, not_3_out, not_4_out, not_5_out, not_6_out, not_7_out, not_8_out, not_9_out,
       not_10_out, not_11_out, not_12_out;

  not not_1 (not_1_out, x);
  not not_2 (not_2_out, y);
  not not_3 (not_3_out, z);
  not not_4 (not_4_out, x);
  not not_5 (not_5_out, y);
  not not_6 (not_6_out, x);
  not not_7 (not_7_out, z);
  not not_8 (not_8_out, x);
  not not_9 (not_9_out, y);
  not not_10 (not_10_out, z);
  not not_11 (not_11_out, y);
  not not_12 (not_12_out, z);
  and and_1 (D7, x, y, z);
  and and_2 (D0, not_1_out, not_2_out, not_3_out);
  and and_3 (D1, not_4_out, not_5_out, z);
  and and_4 (D2, not_6_out, y, not_7_out);
  and and_5 (D3, not_8_out, y, z);
  and and_6 (D4, x, not_9_out, not_10_out);
  and and_7 (D5, x, not_11_out, z);
  and and_8 (D6, x, y, not_12_out);
endmodule
