// Logisim project desiging 1 bit ALU.circ as structural Verilog: 1 circuit, main circuit main
module main (
  input  A,
  input  B,
  input  C,
  input  [1:0] in_4,
  input  Borrow,
  output out_6
);

  wire adder_1_cout, adder_1_out, and_1_out, and_2_out, and_3_out, or_1_out, subtractor_1_bout,
       subtractor_1_out, undriven;

  or or_1 (or_1_out, A, B);
  and and_1 (and_1_out, A, B);
  Adder #(.width(1)) adder_1 (.a(A), .b(B), .out(adder_1_out), .cin(C), .cout(adder_1_cout));
  Subtractor #(.width(1)) subtractor_1 (.a(A), .b(B), .out(subtractor_1_out), .bin(Borrow), .bout(subtractor_1_bout));
  and and_2 (and_2_out, in_4[1], subtractor_1_bout);
  and and_3 (and_3_out, in_4[1], adder_1_cout);
  Multiplexer #(.select(2)) multiplexer_1 (
    .in0(and_1_out), .in1(or_1_out), .in2(adder_1_out), .in3(subtractor_1_out), .out(out_6), .sel(in_4));  // open: en
  Multiplexer multiplexer_2 (.in0(and_3_out), .in1(and_2_out), .sel(in_4[0]), .en(undriven));  // open: out

  // Notes on the sheet:
  //   Figure:Designing an    Arithmetic Logic Unit
  //   A
  //   A
  //   A
  //   01-or
  //   :
  //   10-ADD
  //   11-SuBTRACT
  //   00-AND
  //   A
endmodule
