// Logisim project kuiz2.circ as structural Verilog: 1 circuit, main circuit main
module main (
  input  Cin,
  input  A0,
  input  B0,
  input  [1:0] in_4,
  input  A1,
  input  B1,
  output F0,
  output F1,
  output out_9
);

  wire adder_1_cout, multiplexer_1_out, multiplexer_2_out, not_1_out, not_2_out;

  not not_1 (not_1_out, B1);
  not not_2 (not_2_out, B0);
  Multiplexer #(.select(2)) multiplexer_1 (
    .in0(not_1_out), .in1(1'b0), .in2(1'b1), .in3(B1), .out(multiplexer_1_out), .sel(in_4));  // open: en
  Multiplexer #(.select(2)) multiplexer_2 (
    .in0(not_2_out), .in1(1'b0), .in2(1'b1), .in3(B0), .out(multiplexer_2_out), .sel(in_4));  // open: en
  Adder #(.width(1)) adder_1 (.a(A0), .b(multiplexer_2_out), .out(F0), .cin(Cin), .cout(adder_1_cout));
  Adder #(.width(1)) adder_2 (.a(A1), .b(multiplexer_1_out), .out(F1), .cin(adder_1_cout), .cout(out_9));
endmodule
