// Logisim project uNIVERSAL sHIFT REGISTER2.circ as structural Verilog: 1 circuit, main circuit main
module main (
  input  sERIAL_iNPUT_RIGHT_SHIFT,
  input  i4,
  input  i3,
  input  I2,
  input  SERIAL_INPUT_LEFT_SHIFT,
  input  I1,
  input  [1:0] SELECT_BIT,
  input  CLEAR,
  output A4,
  output A3,
  output A2,
  output A1
);

  wire CLOCK_out, multiplexer_1_out, multiplexer_2_out, multiplexer_3_out, multiplexer_4_out;

  Multiplexer #(.select(2)) multiplexer_1 (
    .in0(A4), .in1(sERIAL_iNPUT_RIGHT_SHIFT), .in2(A3), .in3(i4), .out(multiplexer_1_out), .sel(SELECT_BIT));  // open: en
  Multiplexer #(.select(2)) multiplexer_2 (
    .in0(A3), .in1(A4), .in2(A2), .in3(i3), .out(multiplexer_2_out), .sel(SELECT_BIT));  // open: en
  Multiplexer #(.select(2)) multiplexer_3 (
    .in0(A2), .in1(A3), .in2(A1), .in3(I2), .out(multiplexer_3_out), .sel(SELECT_BIT));  // open: en
  Multiplexer #(.select(2)) multiplexer_4 (
    .in0(A1), .in1(A2), .in2(SERIAL_INPUT_LEFT_SHIFT), .in3(I1), .out(multiplexer_4_out), .sel(SELECT_BIT));  // open: en
  Clock CLOCK (.out(CLOCK_out));
  D_Flip_Flop d_ff_1 (.clk(CLOCK_out), .D(multiplexer_1_out), .Q(A4), .reset(CLEAR));  // open: Qn, preset, en
  D_Flip_Flop d_ff_2 (.clk(CLOCK_out), .D(multiplexer_2_out), .Q(A3), .reset(CLEAR));  // open: Qn, preset, en
  D_Flip_Flop d_ff_3 (.clk(CLOCK_out), .D(multiplexer_3_out), .Q(A2), .reset(CLEAR));  // open: Qn, preset, en
  D_Flip_Flop d_ff_4 (.clk(CLOCK_out), .D(multiplexer_4_out), .Q(A1), .reset(CLEAR));  // open: Qn, preset, en

  // Notes on the sheet:
  //   FIGURE:4 BIT UNIVERSAL SHIFT REGISTER
endmodule
