// Logisim project uNIVERSAL sHIFT rEGISTER.circ as structural Verilog: 1 circuit, main circuit main
module main (
  input  in_1,
  input  [1:0] in_2,
  input  in_3,
  input  SERIAL_INPUT,
  input  I4,
  input  I3,
  input  I2,
  input  I1,
  output A3,
  output A2,
  output A1,
  output A4
);

  wire Clock_out, multiplexer_1_out, multiplexer_2_out, multiplexer_3_out, multiplexer_4_out, not_1_out,
       not_2_out, undriven, undriven_2, undriven_3, undriven_4, undriven_5, undriven_6, undriven_7;

  Clock Clock (.out(Clock_out));
  not not_1 (not_1_out, in_1);
  not not_2 (not_2_out, Clock_out);
  Register #(.width(1)) register_1 (.D(multiplexer_1_out), .Q(A4), .clk(not_2_out), .clr(not_1_out));  // open: en
  Multiplexer #(.select(2)) multiplexer_1 (
    .in0(undriven_2), .in1(SERIAL_INPUT), .in2(undriven_3), .in3(I4), .out(multiplexer_1_out), .sel(in_2),
    .en(undriven));
  Multiplexer #(.select(2)) multiplexer_2 (
    .in0(undriven_3), .in1(undriven_2), .in2(undriven_4), .in3(I3), .out(multiplexer_2_out), .sel(in_2));  // open: en
  Register #(.width(1)) register_2 (.D(multiplexer_2_out), .Q(A3), .clk(not_2_out), .clr(not_1_out));  // open: en
  Register #(.width(1)) register_3 (.D(multiplexer_3_out), .Q(A2), .clk(not_2_out), .clr(not_1_out));  // open: en
  Multiplexer #(.select(2)) multiplexer_3 (
    .in0(undriven_4), .in1(undriven_3), .in2(undriven_6), .in3(I2), .out(multiplexer_3_out), .sel(in_2),
    .en(undriven_5));
  Multiplexer #(.select(2)) multiplexer_4 (
    .in0(undriven_7), .in1(undriven_4), .in2(in_3), .in3(I1), .out(multiplexer_4_out), .sel(in_2));  // open: en
  Register #(.width(1), .trigger("falling")) register_4 (
    .D(multiplexer_4_out), .Q(A1), .clk(not_2_out), .clr(not_1_out));  // open: en
endmodule
